// Logisim project DuckHunt.circ as structural Verilog: 7 circuits, main circuit duckhunt
module duckhunt (
);

  wire clock, clock_keyboard, keyboard_active, standby_mode, start_out;
  wire [3:0] birds_flew_away, misses;
  wire [6:0] keyboard;
  wire [15:0] score;
  wire [31:0] main_duckhunt_1__1, main_duckhunt_1__2, main_duckhunt_1__3, main_duckhunt_1__4,
       main_duckhunt_1__5, main_duckhunt_1__6, main_duckhunt_1__7, main_duckhunt_1__8, main_duckhunt_1__9,
       main_duckhunt_1__10, main_duckhunt_1__11, main_duckhunt_1__12, main_duckhunt_1__13,
       main_duckhunt_1__14, main_duckhunt_1__15, main_duckhunt_1__16, main_duckhunt_1__17,
       main_duckhunt_1__18, main_duckhunt_1__19, main_duckhunt_1__20, main_duckhunt_1__21,
       main_duckhunt_1__22, main_duckhunt_1__23, main_duckhunt_1__24, main_duckhunt_1__25,
       main_duckhunt_1__26, main_duckhunt_1__27, main_duckhunt_1__28, main_duckhunt_1__29,
       main_duckhunt_1__30, main_duckhunt_1__31, main_duckhunt_1__32;

  Clock clock_1 (.out(clock));
  DotMatrix #(.matrixcols(32), .matrixrows(32)) dotmatrix_1 (
    .col0(main_duckhunt_1__32), .col1(main_duckhunt_1__31), .col2(main_duckhunt_1__30),
    .col3(main_duckhunt_1__29), .col4(main_duckhunt_1__28), .col5(main_duckhunt_1__27),
    .col6(main_duckhunt_1__26), .col7(main_duckhunt_1__25), .col8(main_duckhunt_1__24),
    .col9(main_duckhunt_1__23), .col10(main_duckhunt_1__22), .col11(main_duckhunt_1__21),
    .col12(main_duckhunt_1__20), .col13(main_duckhunt_1__19), .col14(main_duckhunt_1__18),
    .col15(main_duckhunt_1__17), .col16(main_duckhunt_1__16), .col17(main_duckhunt_1__15),
    .col18(main_duckhunt_1__14), .col19(main_duckhunt_1__13), .col20(main_duckhunt_1__12),
    .col21(main_duckhunt_1__11), .col22(main_duckhunt_1__10), .col23(main_duckhunt_1__9),
    .col24(main_duckhunt_1__8), .col25(main_duckhunt_1__7), .col26(main_duckhunt_1__6),
    .col27(main_duckhunt_1__5), .col28(main_duckhunt_1__4), .col29(main_duckhunt_1__3),
    .col30(main_duckhunt_1__2), .col31(main_duckhunt_1__1));
  main_duckhunt main_duckhunt_1 (
    .clock(clock), ._1(main_duckhunt_1__1), ._2(main_duckhunt_1__2), ._3(main_duckhunt_1__3),
    ._4(main_duckhunt_1__4), ._5(main_duckhunt_1__5), ._6(main_duckhunt_1__6), ._7(main_duckhunt_1__7),
    ._8(main_duckhunt_1__8), ._9(main_duckhunt_1__9), ._10(main_duckhunt_1__10), ._11(main_duckhunt_1__11),
    ._12(main_duckhunt_1__12), ._13(main_duckhunt_1__13), ._14(main_duckhunt_1__14),
    ._15(main_duckhunt_1__15), ._16(main_duckhunt_1__16), ._17(main_duckhunt_1__17),
    ._18(main_duckhunt_1__18), ._19(main_duckhunt_1__19), ._20(main_duckhunt_1__20),
    ._21(main_duckhunt_1__21), ._22(main_duckhunt_1__22), ._23(main_duckhunt_1__23),
    ._24(main_duckhunt_1__24), ._25(main_duckhunt_1__25), ._26(main_duckhunt_1__26),
    ._27(main_duckhunt_1__27), ._28(main_duckhunt_1__28), ._29(main_duckhunt_1__29),
    ._30(main_duckhunt_1__30), ._31(main_duckhunt_1__31), ._32(main_duckhunt_1__32),
    .clock_keyboard(clock_keyboard), .keyboard_active(keyboard_active), .keyboard(keyboard), .score(score),
    .standby_mode(standby_mode), .bird_flew_away(birds_flew_away), .start(start_out), .missed(misses));
  Keyboard #(.buflen(1)) keyboard_1 (
    .clk(clock_keyboard), .clr(standby_mode), .avail(keyboard_active), .data(keyboard));  // open: re
  LED led_1 (.in(standby_mode));
  Button start (.out(start_out));
  Hex_Digit_Display hex_digit_display_1 (.value(birds_flew_away));  // open: dp
  Hex_Digit_Display hex_digit_display_2 (.value(score[15:12]));  // open: dp
  Hex_Digit_Display hex_digit_display_3 (.value(score[11:8]));  // open: dp
  Hex_Digit_Display hex_digit_display_4 (.value(score[7:4]));  // open: dp
  Hex_Digit_Display hex_digit_display_5 (.value(score[3:0]));  // open: dp
  Hex_Digit_Display hex_digit_display_6 (.value(misses));  // open: dp

  // Notes on the sheet:
  //   birds_flew_away
  //   score
  //   misses
endmodule

module main_duckhunt (
  input  start,
  input  [6:0] keyboard,
  input  keyboard_active,
  input  clock,
  output standby_mode,
  output [31:0] _1,
  output [31:0] _2,
  output [31:0] _3,
  output [31:0] _4,
  output [31:0] _5,
  output [31:0] _6,
  output [31:0] _7,
  output [31:0] _8,
  output [15:0] score,
  output [3:0] missed,
  output [31:0] _9,
  output [31:0] _10,
  output [31:0] _11,
  output [31:0] _12,
  output [31:0] _13,
  output [31:0] _14,
  output [31:0] _15,
  output [31:0] _16,
  output [3:0] bird_flew_away,
  output clock_keyboard,
  output [31:0] _17,
  output [31:0] _18,
  output [31:0] _19,
  output [31:0] _20,
  output [31:0] _21,
  output [31:0] _22,
  output [31:0] _23,
  output [31:0] _24,
  output [31:0] _25,
  output [31:0] _26,
  output [31:0] _27,
  output [31:0] _28,
  output [31:0] _29,
  output [31:0] _30,
  output [31:0] _31,
  output [31:0] _32
);

  wire and_3_out, and_5_out, another_ans, ans_bird, bird_1_ans_bird, comparator_1_eq, \end , gunsught_ans,
       i_o_sel_bird, i_o_sel_gunsight, in_out_bird, in_out_gunsight, keyboard_active_t, kill, not_1_out,
       not_2_out, not_3_out, not_4_out, not_5_out, not_6_out, not_7_out, or_2_out, or_3_out, reset,
       reset_bird, reset_bird_1, to_many_misses;
  wire [5:0] interrupt;
  wire [7:0] bird_adress, gunsight_adress;
  wire [15:0] bird_1_i_o_data_bird_out, bird_subsystem_1_i_o_data_out, controlled_buffer_2_out,
       controlled_buffer_3_out, controlled_buffer_5_out, controlled_buffer_8_out, data_bird, data_gunsight,
       gunsight_1_i_o_data_gunsight_out, gunsight_subsystem_1_out;
  wire [15:4] bird_subsystem_1_birds_flew_away;
  wire [31:0] bird_subsystem_1__1, bird_subsystem_1__2, bird_subsystem_1__3, bird_subsystem_1__4,
       bird_subsystem_1__5, bird_subsystem_1__6, bird_subsystem_1__7, bird_subsystem_1__8,
       bird_subsystem_1__9, bird_subsystem_1__10, bird_subsystem_1__11, bird_subsystem_1__12,
       bird_subsystem_1__13, bird_subsystem_1__14, bird_subsystem_1__15, bird_subsystem_1__16,
       bird_subsystem_1__17, bird_subsystem_1__18, bird_subsystem_1__19, bird_subsystem_1__20,
       bird_subsystem_1__21, bird_subsystem_1__22, bird_subsystem_1__23, bird_subsystem_1__24,
       bird_subsystem_1__25, bird_subsystem_1__26, bird_subsystem_1__27, bird_subsystem_1__28,
       bird_subsystem_1__29, bird_subsystem_1__30, bird_subsystem_1__31, bird_subsystem_1__32,
       gunsight_subsystem_1__1, gunsight_subsystem_1__2, gunsight_subsystem_1__3, gunsight_subsystem_1__4,
       gunsight_subsystem_1__5, gunsight_subsystem_1__6, gunsight_subsystem_1__7, gunsight_subsystem_1__8,
       gunsight_subsystem_1__9, gunsight_subsystem_1__10, gunsight_subsystem_1__11, gunsight_subsystem_1__12,
       gunsight_subsystem_1__13, gunsight_subsystem_1__14, gunsight_subsystem_1__15,
       gunsight_subsystem_1__16, gunsight_subsystem_1__17, gunsight_subsystem_1__18,
       gunsight_subsystem_1__19, gunsight_subsystem_1__20, gunsight_subsystem_1__21,
       gunsight_subsystem_1__22, gunsight_subsystem_1__23, gunsight_subsystem_1__24,
       gunsight_subsystem_1__25, gunsight_subsystem_1__26, gunsight_subsystem_1__27,
       gunsight_subsystem_1__28, gunsight_subsystem_1__29, gunsight_subsystem_1__30,
       gunsight_subsystem_1__31, gunsight_subsystem_1__32;

  and and_1 (ans_bird, bird_1_ans_bird, kill);
  and and_2 (another_ans, bird_1_ans_bird, to_many_misses);
  or or_1 (reset_bird_1, another_ans, reset_bird);
  Multiplexer #(.width(6), .disabled(0), .enable("false")) multiplexer_1 (
    .in0(6'b000101), .in1(6'b000110), .out(interrupt), .sel(to_many_misses));
  or or_2 (or_2_out, to_many_misses, kill);
  shot shot_1 (
    ._1_bird(bird_subsystem_1__1), ._9_bird(bird_subsystem_1__9), ._17_bird(bird_subsystem_1__17),
    ._25_bird(bird_subsystem_1__25), ._2_bird(bird_subsystem_1__2), ._10_bird(bird_subsystem_1__10),
    ._18_bird(bird_subsystem_1__18), ._26_bird(bird_subsystem_1__26), ._3_bird(bird_subsystem_1__3),
    ._11_bird(bird_subsystem_1__11), ._19_bird(bird_subsystem_1__19), ._27_bird(bird_subsystem_1__27),
    ._4_bird(bird_subsystem_1__4), ._12_bird(bird_subsystem_1__12), ._20_bird(bird_subsystem_1__20),
    ._28_bird(bird_subsystem_1__28), ._5_bird(bird_subsystem_1__5), ._21_bird(bird_subsystem_1__21),
    ._29_bird(bird_subsystem_1__29), ._6_bird(bird_subsystem_1__6), ._14_bird(bird_subsystem_1__14),
    ._22_bird(bird_subsystem_1__22), ._30_bird(bird_subsystem_1__30), ._7_bird(bird_subsystem_1__7),
    ._15_bird(bird_subsystem_1__15), ._23_bird(bird_subsystem_1__23), ._31_bird(bird_subsystem_1__31),
    ._8_bird(bird_subsystem_1__8), ._16_bird(bird_subsystem_1__16), ._24_bird(bird_subsystem_1__24),
    ._32_bird(bird_subsystem_1__32), ._1_gunsight(gunsight_subsystem_1__1),
    ._2_gunsight(gunsight_subsystem_1__2), ._3_gunsight(gunsight_subsystem_1__3),
    ._4_gunsight(gunsight_subsystem_1__4), ._5_gunsight(gunsight_subsystem_1__5),
    ._6_gunsight(gunsight_subsystem_1__6), ._7_gunsight(gunsight_subsystem_1__7),
    ._8_gunsight(gunsight_subsystem_1__8), ._9_gunsight(gunsight_subsystem_1__9),
    ._10_gunsight(gunsight_subsystem_1__10), ._11_gunsight(gunsight_subsystem_1__11),
    ._12_gunsight(gunsight_subsystem_1__12), ._13_gunsight(gunsight_subsystem_1__13),
    ._14_gunsight(gunsight_subsystem_1__14), ._15_gunsight(gunsight_subsystem_1__15),
    ._16_gunsight(gunsight_subsystem_1__16), ._17_gunsight(gunsight_subsystem_1__17),
    ._18_gunsight(gunsight_subsystem_1__18), ._19_gunsight(gunsight_subsystem_1__19),
    ._20_gunsight(gunsight_subsystem_1__20), ._21_gunsight(gunsight_subsystem_1__21),
    ._22_gunsight(gunsight_subsystem_1__22), ._23_gunsight(gunsight_subsystem_1__23),
    ._24_gunsight(gunsight_subsystem_1__24), ._25_gunsight(gunsight_subsystem_1__25),
    ._26_gunsight(gunsight_subsystem_1__26), ._27_gunsight(gunsight_subsystem_1__27),
    ._28_gunsight(gunsight_subsystem_1__28), ._29_gunsight(gunsight_subsystem_1__29),
    ._30_gunsight(gunsight_subsystem_1__30), ._31_gunsight(gunsight_subsystem_1__31),
    ._32_gunsight(gunsight_subsystem_1__32), ._13_bird(bird_subsystem_1__13), ._2(_2), ._3(_3), ._4(_4),
    ._5(_5), ._6(_6), ._7(_7), ._8(_8), ._9(_9), ._10(_10), ._11(_11), ._12(_12), ._13(_13), ._14(_14),
    ._15(_15), ._16(_16), ._17(_17), ._18(_18), ._19(_19), ._20(_20), ._21(_21), ._22(_22), ._23(_23),
    ._24(_24), ._25(_25), ._26(_26), ._27(_27), ._28(_28), ._29(_29), ._30(_30), ._31(_31), ._32(_32),
    ._1(_1), .KILL(kill), .shot(comparator_1_eq), .bird_ans(ans_bird), .reset_bird(reset_bird),
    .misses(missed), .too_many_misses(to_many_misses), .clear(reset));
  not not_1 (not_1_out, in_out_bird);
  assign data_bird = not_1_out ? bird_1_i_o_data_bird_out : 16'bz;  // Controlled_Buffer controlled_buffer_1
  bird bird_1 (
    .bird_adress(bird_adress), .i_o_sel_bird(i_o_sel_bird), .i_o_data_bird_out(bird_1_i_o_data_bird_out),
    .IRQ(or_2_out), .in_out_bird(in_out_bird), .i_o_data_bird_in(controlled_buffer_3_out),
    .ans_bird(bird_1_ans_bird), .hold(standby_mode), .int_vector(interrupt), .clock(clock), .reset(reset));
  assign controlled_buffer_2_out = not_2_out ? data_bird : 16'bz;  // Controlled_Buffer controlled_buffer_2
  assign controlled_buffer_3_out = in_out_bird ? data_bird : 16'bz;  // Controlled_Buffer controlled_buffer_3
  bird_subsystem bird_subsystem_1 (
    .in_out(in_out_bird), .i_o_data(controlled_buffer_2_out), .i_o_sel(i_o_sel_bird),
    .i_o_adress(bird_adress), .i_o_data_out(bird_subsystem_1_i_o_data_out), ._1(bird_subsystem_1__1),
    ._19(bird_subsystem_1__19), ._18(bird_subsystem_1__18), ._2(bird_subsystem_1__2),
    ._20(bird_subsystem_1__20), ._17(bird_subsystem_1__17), ._21(bird_subsystem_1__21),
    ._16(bird_subsystem_1__16), ._3(bird_subsystem_1__3), ._22(bird_subsystem_1__22),
    ._15(bird_subsystem_1__15), ._4(bird_subsystem_1__4), ._23(bird_subsystem_1__23),
    ._14(bird_subsystem_1__14), ._5(bird_subsystem_1__5), ._24(bird_subsystem_1__24), .clock(clock),
    ._13(bird_subsystem_1__13), ._6(bird_subsystem_1__6), ._25(bird_subsystem_1__25),
    ._32(bird_subsystem_1__32), ._12(bird_subsystem_1__12), ._7(bird_subsystem_1__7),
    ._31(bird_subsystem_1__31), ._26(bird_subsystem_1__26), ._8(bird_subsystem_1__8),
    ._11(bird_subsystem_1__11), ._30(bird_subsystem_1__30), ._27(bird_subsystem_1__27),
    ._10(bird_subsystem_1__10), ._9(bird_subsystem_1__9), ._29(bird_subsystem_1__29),
    ._28(bird_subsystem_1__28), .reset_bird(reset_bird_1), .score(score),
    .birds_flew_away({bird_subsystem_1_birds_flew_away, bird_flew_away}), .\end (\end ), .reset_all(reset));
  not not_2 (not_2_out, in_out_bird);
  assign data_bird = in_out_bird ? bird_subsystem_1_i_o_data_out : 16'bz;  // Controlled_Buffer controlled_buffer_4
  not not_3 (not_3_out, in_out_gunsight);
  assign controlled_buffer_5_out = not_3_out ? data_gunsight : 16'bz;  // Controlled_Buffer controlled_buffer_5
  or or_3 (or_3_out, to_many_misses, \end );
  gunsight_subsystem gunsight_subsystem_1 (
    ._1(gunsight_subsystem_1__1), ._19(gunsight_subsystem_1__19), ._18(gunsight_subsystem_1__18),
    ._2(gunsight_subsystem_1__2), ._20(gunsight_subsystem_1__20), ._17(gunsight_subsystem_1__17),
    ._21(gunsight_subsystem_1__21), ._16(gunsight_subsystem_1__16), ._3(gunsight_subsystem_1__3),
    ._22(gunsight_subsystem_1__22), ._15(gunsight_subsystem_1__15), ._4(gunsight_subsystem_1__4),
    ._23(gunsight_subsystem_1__23), ._14(gunsight_subsystem_1__14), ._5(gunsight_subsystem_1__5),
    .keyboard_active(keyboard_active_t), .keyboard(keyboard), ._24(gunsight_subsystem_1__24),
    ._13(gunsight_subsystem_1__13), ._6(gunsight_subsystem_1__6), ._25(gunsight_subsystem_1__25),
    ._32(gunsight_subsystem_1__32), ._12(gunsight_subsystem_1__12), ._7(gunsight_subsystem_1__7),
    ._26(gunsight_subsystem_1__26), ._31(gunsight_subsystem_1__31), ._8(gunsight_subsystem_1__8),
    ._11(gunsight_subsystem_1__11), ._30(gunsight_subsystem_1__30), ._27(gunsight_subsystem_1__27),
    ._10(gunsight_subsystem_1__10), ._9(gunsight_subsystem_1__9), ._29(gunsight_subsystem_1__29),
    ._28(gunsight_subsystem_1__28), .out(gunsight_subsystem_1_out), .in_out(in_out_gunsight),
    .i_o_data_control(controlled_buffer_5_out), .i_o_sel(i_o_sel_gunsight), .i_o_adress(gunsight_adress),
    .gunsight_ans(gunsught_ans));
  assign data_gunsight = in_out_gunsight ? gunsight_subsystem_1_out : 16'bz;  // Controlled_Buffer controlled_buffer_6
  not not_4 (not_4_out, in_out_gunsight);
  assign data_gunsight = not_4_out ? gunsight_1_i_o_data_gunsight_out : 16'bz;  // Controlled_Buffer controlled_buffer_7
  assign controlled_buffer_8_out = in_out_gunsight ? data_gunsight : 16'bz;  // Controlled_Buffer controlled_buffer_8
  gunsight gunsight_1 (
    .endgame(or_3_out), .gunsight_ans(gunsught_ans), .hold(standby_mode),
    .i_o_adress_gunsight(gunsight_adress), .i_o_sel_gunsight(i_o_sel_gunsight),
    .i_o_data_gunsight_out(gunsight_1_i_o_data_gunsight_out), .i_o_data_gunsight_in(controlled_buffer_8_out),
    .clock(clock), .in_out_gunsight(in_out_gunsight), .reset(reset));
  not not_5 (not_5_out, start);
  and and_3 (and_3_out, not_5_out, start);
  Comparator #(.width(7), .mode("unsigned")) comparator_1 (
    .a(7'b0001010), .b(keyboard), .eq(comparator_1_eq));  // open: gt, lt
  and and_4 (keyboard_active_t, clock, keyboard_active);
  and and_5 (and_5_out, not_6_out, gunsught_ans);
  not not_6 (not_6_out, gunsught_ans);
  S_R_Flip_Flop #(.trigger("low")) s_r_ff_1 (
    .S(and_3_out), .clk(1'b0), .R(and_5_out), .Qn(standby_mode));  // open: Q, preset, reset, en
  not not_7 (not_7_out, standby_mode);
  and and_6 (clock_keyboard, i_o_sel_gunsight, in_out_gunsight);
  and and_7 (reset, not_7_out, standby_mode);

  // Other names for the same wires on the sheet: hold = standby_mode
endmodule

module bird (
  input  IRQ,
  input  [5:0] int_vector,
  input  hold,
  input  clock,
  input  reset,
  input  [15:0] i_o_data_bird_in,
  output ans_bird,
  output in_out_bird,
  output [7:0] bird_adress,
  output i_o_sel_bird,
  output [15:0] i_o_data_bird_out
);

  wire cdm16_1_data_ins_prime, cdm16_1_mem, code, data, nand_1_out, not_1_out, RAM, word;
  wire [15:0] cdm16_1_data_out, controlled_buffer_2_out;
  wire [15:8] cdm16_1_address;

  cdm16 cdm16_1 (
    .IRQ(IRQ), .int_vec(int_vector), .hold(hold), .mem(cdm16_1_mem), .data_ins_prime(cdm16_1_data_ins_prime),
    .rd_wr_prime(in_out_bird), .address({cdm16_1_address, bird_adress}), .word(word),
    .data_out(cdm16_1_data_out), .data_in(controlled_buffer_2_out), .clock(clock), .IAck(ans_bird));  // open: EXC, exc_vec, R0, R1, R2, R3, R4, R5, R6, FP, PC, PS, SP, status, fetch
  and and_1 (i_o_sel_bird, ~nand_1_out, clock, data);  // AND_Gate
  // Probe on cdm16_1_data_out
  assign i_o_data_bird_in = not_1_out ? cdm16_1_data_out : 16'bz;  // Controlled_Buffer controlled_buffer_1
  not not_1 (not_1_out, in_out_bird);
  assign controlled_buffer_2_out = in_out_bird ? i_o_data_bird_in : 16'bz;  // Controlled_Buffer controlled_buffer_2
  // Probe on controlled_buffer_2_out
  // Probe on i_o_data_bird_in
  nand nand_1 (nand_1_out, cdm16_1_address[8], cdm16_1_address[9], cdm16_1_address[10], cdm16_1_address[11], cdm16_1_address[12], cdm16_1_address[13], cdm16_1_address[14], cdm16_1_address[15]);
  and and_2 (RAM, nand_1_out, data);
  Decoder #(.disabled(0)) decoder_1 (.out0(code), .out1(data), .sel(cdm16_1_data_ins_prime), .en(cdm16_1_mem));
  Pull_Resistor pull_resistor_1 (.node(bird_adress[0]));
  Pull_Resistor pull_resistor_2 (.node(bird_adress[1]));
  Pull_Resistor pull_resistor_3 (.node(bird_adress[2]));
  Pull_Resistor pull_resistor_4 (.node(bird_adress[3]));
  Pull_Resistor pull_resistor_5 (.node(bird_adress[4]));
  Pull_Resistor pull_resistor_6 (.node(bird_adress[5]));
  Pull_Resistor pull_resistor_7 (.node(bird_adress[6]));
  Pull_Resistor pull_resistor_8 (.node(bird_adress[7]));
  Pull_Resistor pull_resistor_9 (.node(cdm16_1_address[8]));
  Pull_Resistor pull_resistor_10 (.node(cdm16_1_address[9]));
  Pull_Resistor pull_resistor_11 (.node(cdm16_1_address[10]));
  Pull_Resistor pull_resistor_12 (.node(cdm16_1_address[11]));
  Pull_Resistor pull_resistor_13 (.node(cdm16_1_address[12]));
  Pull_Resistor pull_resistor_14 (.node(cdm16_1_address[13]));
  Pull_Resistor pull_resistor_15 (.node(cdm16_1_address[14]));
  Pull_Resistor pull_resistor_16 (.node(cdm16_1_address[15]));
  // ROM rom_1: pin names not known; wires that end beside it: {cdm16_1_address, bird_adress}, code, word, i_o_data_bird_in
  // RAM ram_1: pin names not known; wires that end beside it: {cdm16_1_address, bird_adress}, word, RAM, clock, in_out_bird, reset, i_o_data_bird_in

  assign i_o_data_bird_out = i_o_data_bird_in;

  // Other names for the same wires on the sheet: clk = clock; read_write = in_out_bird
endmodule

module gunsight (
  input  endgame,
  input  hold,
  input  clock,
  input  reset,
  input  [15:0] i_o_data_gunsight_in,
  output gunsight_ans,
  output in_out_gunsight,
  output [7:0] i_o_adress_gunsight,
  output i_o_sel_gunsight,
  output [15:0] i_o_data_gunsight_out
);

  wire cdm16_1_data_ins_prime, cdm16_1_mem, code, data, nand_1_out, not_1_out, RAM, word;
  wire [15:0] cdm16_1_data_out, controlled_buffer_2_out;
  wire [15:8] cdm16_1_address;

  cdm16 cdm16_1 (
    .IRQ(endgame), .int_vec(6'b000101), .hold(hold), .mem(cdm16_1_mem),
    .data_ins_prime(cdm16_1_data_ins_prime), .rd_wr_prime(in_out_gunsight),
    .address({cdm16_1_address, i_o_adress_gunsight}), .word(word), .data_out(cdm16_1_data_out),
    .data_in(controlled_buffer_2_out), .clock(clock), .IAck(gunsight_ans));  // open: EXC, exc_vec, R0, R1, R2, R3, R4, R5, R6, FP, PC, PS, SP, status, fetch
  and and_1 (i_o_sel_gunsight, ~nand_1_out, clock, data);  // AND_Gate
  assign i_o_data_gunsight_in = not_1_out ? cdm16_1_data_out : 16'bz;  // Controlled_Buffer controlled_buffer_1
  not not_1 (not_1_out, in_out_gunsight);
  assign controlled_buffer_2_out = in_out_gunsight ? i_o_data_gunsight_in : 16'bz;  // Controlled_Buffer controlled_buffer_2
  and and_2 (RAM, nand_1_out, data);
  Decoder #(.disabled(0)) decoder_1 (.out0(code), .out1(data), .sel(cdm16_1_data_ins_prime), .en(cdm16_1_mem));
  nand nand_1 (nand_1_out, cdm16_1_address[8], cdm16_1_address[9], cdm16_1_address[10], cdm16_1_address[11], cdm16_1_address[12], cdm16_1_address[13], cdm16_1_address[14], cdm16_1_address[15]);
  Pull_Resistor pull_resistor_1 (.node(i_o_adress_gunsight[0]));
  Pull_Resistor pull_resistor_2 (.node(i_o_adress_gunsight[1]));
  Pull_Resistor pull_resistor_3 (.node(i_o_adress_gunsight[2]));
  Pull_Resistor pull_resistor_4 (.node(i_o_adress_gunsight[3]));
  Pull_Resistor pull_resistor_5 (.node(i_o_adress_gunsight[4]));
  Pull_Resistor pull_resistor_6 (.node(i_o_adress_gunsight[5]));
  Pull_Resistor pull_resistor_7 (.node(i_o_adress_gunsight[6]));
  Pull_Resistor pull_resistor_8 (.node(i_o_adress_gunsight[7]));
  Pull_Resistor pull_resistor_9 (.node(cdm16_1_address[8]));
  Pull_Resistor pull_resistor_10 (.node(cdm16_1_address[9]));
  Pull_Resistor pull_resistor_11 (.node(cdm16_1_address[10]));
  Pull_Resistor pull_resistor_12 (.node(cdm16_1_address[11]));
  Pull_Resistor pull_resistor_13 (.node(cdm16_1_address[12]));
  Pull_Resistor pull_resistor_14 (.node(cdm16_1_address[13]));
  Pull_Resistor pull_resistor_15 (.node(cdm16_1_address[14]));
  Pull_Resistor pull_resistor_16 (.node(cdm16_1_address[15]));
  // ROM rom_1: pin names not known; wires that end beside it: {cdm16_1_address, i_o_adress_gunsight}, code, word, i_o_data_gunsight_in
  // RAM ram_1: pin names not known; wires that end beside it: {cdm16_1_address, i_o_adress_gunsight}, word, RAM, clock, in_out_gunsight, reset, i_o_data_gunsight_in

  assign i_o_data_gunsight_out = i_o_data_gunsight_in;

  // Other names for the same wires on the sheet: clk = clock; read_write = in_out_gunsight
endmodule

module bird_subsystem (
  input  reset_bird,
  input  reset_all,
  input  in_out,
  input  [15:0] i_o_data,
  input  i_o_sel,
  input  [7:0] i_o_adress,
  input  clock,
  output [15:0] i_o_data_out,
  output [31:0] _1,
  output [31:0] _19,
  output [31:0] _18,
  output [31:0] _2,
  output [31:0] _20,
  output [31:0] _17,
  output [31:0] _21,
  output [31:0] _16,
  output [31:0] _3,
  output \end ,
  output [31:0] _22,
  output [31:0] _15,
  output [31:0] _4,
  output [15:0] birds_flew_away,
  output [15:0] score,
  output [31:0] _23,
  output [31:0] _14,
  output [31:0] _5,
  output [31:0] _24,
  output [31:0] _13,
  output [31:0] _6,
  output [31:0] _25,
  output [31:0] _32,
  output [31:0] _12,
  output [31:0] _7,
  output [31:0] _31,
  output [31:0] _26,
  output [31:0] _8,
  output [31:0] _11,
  output [31:0] _30,
  output [31:0] _27,
  output [31:0] _10,
  output [31:0] _9,
  output [31:0] _29,
  output [31:0] _28
);

  wire _0_out, _2_out, _4_out, _6_out, _8_out, _10_out, _12_out, _14_out, _16_out, _18_out, _20_out, _22_out,
       _24_out, _26_out, _28_out, _30_out, _32_out, _34_out, _36_out, _38_out, _40_out, _42_out, _44_out,
       _46_out, _48_out, _50_out, _52_out, _54_out, _56_out, _58_out, _60_out, _62_out, _64_out, _66_out,
       _68_out, _70_out, _72_out, _74_out, _76_out, _78_out, _80_out, _82_out, _84_out, _86_out, _88_out,
       _90_out, _92_out, _94_out, _96_out, _98_out, _100_out, _102_out, _104_out, _106_out, _108_out,
       _110_out, _112_out, _114_out, _116_out, _118_out, _120_out, _122_out, _124_out, _126_out, _128_out,
       _160_out, _164_out, _166_out, comparator_1_eq, comparator_2_eq, comparator_3_eq, comparator_4_eq,
       comparator_5_eq, comparator_6_eq, comparator_7_eq, comparator_8_eq, comparator_9_eq, comparator_10_eq,
       comparator_11_eq, comparator_12_eq, comparator_13_eq, comparator_14_eq, comparator_15_eq,
       comparator_16_eq, comparator_17_eq, comparator_18_eq, comparator_19_eq, comparator_20_eq,
       comparator_21_eq, comparator_22_eq, comparator_23_eq, comparator_24_eq, comparator_25_eq,
       comparator_26_eq, comparator_27_eq, comparator_28_eq, comparator_29_eq, comparator_30_eq,
       comparator_31_eq, comparator_32_eq, comparator_33_eq, comparator_34_eq, comparator_35_eq,
       comparator_36_eq, comparator_37_eq, comparator_38_eq, comparator_39_eq, comparator_40_eq,
       comparator_41_eq, comparator_42_eq, comparator_43_eq, comparator_44_eq, comparator_45_eq,
       comparator_46_eq, comparator_47_eq, comparator_48_eq, comparator_49_eq, comparator_50_eq,
       comparator_51_eq, comparator_52_eq, comparator_53_eq, comparator_54_eq, comparator_55_eq,
       comparator_56_eq, comparator_57_eq, comparator_58_eq, comparator_59_eq, comparator_60_eq,
       comparator_61_eq, comparator_62_eq, comparator_63_eq, comparator_64_eq, comparator_65_eq,
       comparator_66_eq, comparator_67_eq, comparator_68_eq, decoder_1_out0, decoder_1_out1, decoder_2_out0,
       decoder_2_out1, decoder_3_out0, decoder_3_out1, decoder_4_out0, decoder_4_out1, decoder_5_out0,
       decoder_5_out1, decoder_6_out0, decoder_6_out1, decoder_7_out0, decoder_7_out1, decoder_8_out0,
       decoder_8_out1, decoder_9_out0, decoder_9_out1, decoder_10_out0, decoder_10_out1, decoder_11_out0,
       decoder_11_out1, decoder_12_out0, decoder_12_out1, decoder_13_out0, decoder_13_out1, decoder_14_out0,
       decoder_14_out1, decoder_15_out0, decoder_15_out1, decoder_16_out0, decoder_16_out1, decoder_17_out0,
       decoder_17_out1, decoder_18_out0, decoder_18_out1, decoder_19_out0, decoder_19_out1, decoder_20_out0,
       decoder_20_out1, decoder_21_out0, decoder_21_out1, decoder_22_out0, decoder_22_out1, decoder_23_out0,
       decoder_23_out1, decoder_24_out0, decoder_24_out1, decoder_25_out0, decoder_25_out1, decoder_26_out0,
       decoder_26_out1, decoder_27_out0, decoder_27_out1, decoder_28_out0, decoder_28_out1, decoder_29_out0,
       decoder_29_out1, decoder_30_out0, decoder_30_out1, decoder_31_out0, decoder_31_out1, decoder_32_out0,
       decoder_32_out1, decoder_33_out0, decoder_33_out1, decoder_34_out0, decoder_34_out1, decoder_35_out0,
       decoder_35_out1, decoder_36_out0, decoder_36_out1, decoder_37_out0, decoder_37_out1, decoder_38_out0,
       decoder_38_out1, decoder_39_out0, decoder_39_out1, decoder_40_out0, decoder_40_out1, decoder_41_out0,
       decoder_41_out1, decoder_42_out0, decoder_42_out1, decoder_43_out0, decoder_43_out1, decoder_44_out0,
       decoder_44_out1, decoder_45_out0, decoder_45_out1, decoder_46_out0, decoder_46_out1, decoder_47_out0,
       decoder_47_out1, decoder_48_out0, decoder_48_out1, decoder_49_out0, decoder_49_out1, decoder_50_out0,
       decoder_50_out1, decoder_51_out0, decoder_51_out1, decoder_52_out0, decoder_52_out1, decoder_53_out0,
       decoder_53_out1, decoder_54_out0, decoder_54_out1, decoder_55_out0, decoder_55_out1, decoder_56_out0,
       decoder_56_out1, decoder_57_out0, decoder_57_out1, decoder_58_out0, decoder_58_out1, decoder_59_out0,
       decoder_59_out1, decoder_60_out1, decoder_61_out0, decoder_61_out1, decoder_62_out0, decoder_62_out1,
       decoder_63_out0, decoder_63_out1, decoder_64_out0, decoder_64_out1, decoder_65_out0, decoder_65_out1,
       decoder_66_out0, decoder_66_out1, decoder_67_out0, decoder_67_out1, decoder_68_out0, decoder_68_out1,
       reset;
  wire [15:0] random_1_out;
  wire [15:1] register_57_q;

  Register #(.width(16)) register_1 (
    .D(i_o_data),
    .Q({_2[0], _2[1], _2[2], _2[3], _2[4], _2[5], _2[6], _2[7], _2[8], _2[9], _2[10], _2[11], _2[12], _2[13], _2[14], _2[15]}),
    .clk(decoder_3_out0), .clr(reset));  // open: en
  Register #(.width(16)) register_2 (
    .D(i_o_data),
    .Q({_3[0], _3[1], _3[2], _3[3], _3[4], _3[5], _3[6], _3[7], _3[8], _3[9], _3[10], _3[11], _3[12], _3[13], _3[14], _3[15]}),
    .clk(decoder_5_out0), .clr(reset));  // open: en
  Register #(.width(16)) register_3 (
    .D(i_o_data),
    .Q({_4[0], _4[1], _4[2], _4[3], _4[4], _4[5], _4[6], _4[7], _4[8], _4[9], _4[10], _4[11], _4[12], _4[13], _4[14], _4[15]}),
    .clk(decoder_7_out0), .clr(reset));  // open: en
  Register #(.width(16)) register_4 (
    .D(i_o_data),
    .Q({_5[0], _5[1], _5[2], _5[3], _5[4], _5[5], _5[6], _5[7], _5[8], _5[9], _5[10], _5[11], _5[12], _5[13], _5[14], _5[15]}),
    .clk(decoder_9_out0), .clr(reset));  // open: en
  Register #(.width(16)) register_5 (
    .D(i_o_data),
    .Q({_6[0], _6[1], _6[2], _6[3], _6[4], _6[5], _6[6], _6[7], _6[8], _6[9], _6[10], _6[11], _6[12], _6[13], _6[14], _6[15]}),
    .clk(decoder_11_out0), .clr(reset));  // open: en
  Register #(.width(16)) register_6 (
    .D(i_o_data),
    .Q({_7[0], _7[1], _7[2], _7[3], _7[4], _7[5], _7[6], _7[7], _7[8], _7[9], _7[10], _7[11], _7[12], _7[13], _7[14], _7[15]}),
    .clk(decoder_13_out0), .clr(reset));  // open: en
  Register #(.width(16)) register_7 (
    .D(i_o_data),
    .Q({_8[0], _8[1], _8[2], _8[3], _8[4], _8[5], _8[6], _8[7], _8[8], _8[9], _8[10], _8[11], _8[12], _8[13], _8[14], _8[15]}),
    .clk(decoder_15_out0), .clr(reset));  // open: en
  Register #(.width(16)) register_8 (
    .D(i_o_data),
    .Q({_9[0], _9[1], _9[2], _9[3], _9[4], _9[5], _9[6], _9[7], _9[8], _9[9], _9[10], _9[11], _9[12], _9[13], _9[14], _9[15]}),
    .clk(decoder_17_out0), .clr(reset));  // open: en
  Register #(.width(16)) register_9 (
    .D(i_o_data),
    .Q({_1[0], _1[1], _1[2], _1[3], _1[4], _1[5], _1[6], _1[7], _1[8], _1[9], _1[10], _1[11], _1[12], _1[13], _1[14], _1[15]}),
    .clk(decoder_1_out0), .clr(reset));  // open: en
  Register #(.width(16)) register_10 (
    .D(i_o_data),
    .Q({_1[16], _1[17], _1[18], _1[19], _1[20], _1[21], _1[22], _1[23], _1[24], _1[25], _1[26], _1[27], _1[28], _1[29], _1[30], _1[31]}),
    .clk(decoder_2_out0), .clr(reset));  // open: en
  assign i_o_data = decoder_3_out1 ? {_2[0], _2[1], _2[2], _2[3], _2[4], _2[5], _2[6], _2[7], _2[8], _2[9], _2[10], _2[11], _2[12], _2[13], _2[14], _2[15]} : 16'bz;  // Controlled_Buffer controlled_buffer_1
  Register #(.width(16)) register_11 (
    .D(i_o_data),
    .Q({_2[16], _2[17], _2[18], _2[19], _2[20], _2[21], _2[22], _2[23], _2[24], _2[25], _2[26], _2[27], _2[28], _2[29], _2[30], _2[31]}),
    .clk(decoder_4_out0), .clr(reset));  // open: en
  assign i_o_data = decoder_5_out1 ? {_3[0], _3[1], _3[2], _3[3], _3[4], _3[5], _3[6], _3[7], _3[8], _3[9], _3[10], _3[11], _3[12], _3[13], _3[14], _3[15]} : 16'bz;  // Controlled_Buffer controlled_buffer_2
  Register #(.width(16)) register_12 (
    .D(i_o_data),
    .Q({_3[16], _3[17], _3[18], _3[19], _3[20], _3[21], _3[22], _3[23], _3[24], _3[25], _3[26], _3[27], _3[28], _3[29], _3[30], _3[31]}),
    .clk(decoder_6_out0), .clr(reset));  // open: en
  assign i_o_data = decoder_7_out1 ? {_4[0], _4[1], _4[2], _4[3], _4[4], _4[5], _4[6], _4[7], _4[8], _4[9], _4[10], _4[11], _4[12], _4[13], _4[14], _4[15]} : 16'bz;  // Controlled_Buffer controlled_buffer_3
  Register #(.width(16)) register_13 (
    .D(i_o_data),
    .Q({_4[16], _4[17], _4[18], _4[19], _4[20], _4[21], _4[22], _4[23], _4[24], _4[25], _4[26], _4[27], _4[28], _4[29], _4[30], _4[31]}),
    .clk(decoder_8_out0), .clr(reset));  // open: en
  assign i_o_data = decoder_9_out1 ? {_5[0], _5[1], _5[2], _5[3], _5[4], _5[5], _5[6], _5[7], _5[8], _5[9], _5[10], _5[11], _5[12], _5[13], _5[14], _5[15]} : 16'bz;  // Controlled_Buffer controlled_buffer_4
  Register #(.width(16)) register_14 (
    .D(i_o_data),
    .Q({_5[16], _5[17], _5[18], _5[19], _5[20], _5[21], _5[22], _5[23], _5[24], _5[25], _5[26], _5[27], _5[28], _5[29], _5[30], _5[31]}),
    .clk(decoder_10_out0), .clr(reset));  // open: en
  assign i_o_data = decoder_11_out1 ? {_6[0], _6[1], _6[2], _6[3], _6[4], _6[5], _6[6], _6[7], _6[8], _6[9], _6[10], _6[11], _6[12], _6[13], _6[14], _6[15]} : 16'bz;  // Controlled_Buffer controlled_buffer_5
  Register #(.width(16)) register_15 (
    .D(i_o_data),
    .Q({_6[16], _6[17], _6[18], _6[19], _6[20], _6[21], _6[22], _6[23], _6[24], _6[25], _6[26], _6[27], _6[28], _6[29], _6[30], _6[31]}),
    .clk(decoder_12_out0), .clr(reset));  // open: en
  assign i_o_data = decoder_13_out1 ? {_7[0], _7[1], _7[2], _7[3], _7[4], _7[5], _7[6], _7[7], _7[8], _7[9], _7[10], _7[11], _7[12], _7[13], _7[14], _7[15]} : 16'bz;  // Controlled_Buffer controlled_buffer_6
  Register #(.width(16)) register_16 (
    .D(i_o_data),
    .Q({_7[16], _7[17], _7[18], _7[19], _7[20], _7[21], _7[22], _7[23], _7[24], _7[25], _7[26], _7[27], _7[28], _7[29], _7[30], _7[31]}),
    .clk(decoder_14_out0), .clr(reset));  // open: en
  assign i_o_data = decoder_15_out1 ? {_8[0], _8[1], _8[2], _8[3], _8[4], _8[5], _8[6], _8[7], _8[8], _8[9], _8[10], _8[11], _8[12], _8[13], _8[14], _8[15]} : 16'bz;  // Controlled_Buffer controlled_buffer_7
  Register #(.width(16)) register_17 (
    .D(i_o_data),
    .Q({_8[16], _8[17], _8[18], _8[19], _8[20], _8[21], _8[22], _8[23], _8[24], _8[25], _8[26], _8[27], _8[28], _8[29], _8[30], _8[31]}),
    .clk(decoder_16_out0), .clr(reset));  // open: en
  assign i_o_data = decoder_17_out1 ? {_9[0], _9[1], _9[2], _9[3], _9[4], _9[5], _9[6], _9[7], _9[8], _9[9], _9[10], _9[11], _9[12], _9[13], _9[14], _9[15]} : 16'bz;  // Controlled_Buffer controlled_buffer_8
  Register #(.width(16)) register_18 (
    .D(i_o_data),
    .Q({_9[16], _9[17], _9[18], _9[19], _9[20], _9[21], _9[22], _9[23], _9[24], _9[25], _9[26], _9[27], _9[28], _9[29], _9[30], _9[31]}),
    .clk(decoder_18_out0), .clr(reset));  // open: en
  assign i_o_data = decoder_1_out1 ? {_1[0], _1[1], _1[2], _1[3], _1[4], _1[5], _1[6], _1[7], _1[8], _1[9], _1[10], _1[11], _1[12], _1[13], _1[14], _1[15]} : 16'bz;  // Controlled_Buffer controlled_buffer_9
  Decoder #(.disabled(0)) decoder_1 (.out0(decoder_1_out0), .out1(decoder_1_out1), .sel(in_out), .en(_0_out));
  Decoder #(.disabled(0)) decoder_2 (.out0(decoder_2_out0), .out1(decoder_2_out1), .sel(in_out), .en(_2_out));
  assign i_o_data = decoder_2_out1 ? {_1[16], _1[17], _1[18], _1[19], _1[20], _1[21], _1[22], _1[23], _1[24], _1[25], _1[26], _1[27], _1[28], _1[29], _1[30], _1[31]} : 16'bz;  // Controlled_Buffer controlled_buffer_10
  Decoder #(.disabled(0)) decoder_3 (.out0(decoder_3_out0), .out1(decoder_3_out1), .sel(in_out), .en(_4_out));
  Decoder #(.disabled(0)) decoder_4 (.out0(decoder_4_out0), .out1(decoder_4_out1), .sel(in_out), .en(_6_out));
  assign i_o_data = decoder_4_out1 ? {_2[16], _2[17], _2[18], _2[19], _2[20], _2[21], _2[22], _2[23], _2[24], _2[25], _2[26], _2[27], _2[28], _2[29], _2[30], _2[31]} : 16'bz;  // Controlled_Buffer controlled_buffer_11
  Decoder #(.disabled(0)) decoder_5 (.out0(decoder_5_out0), .out1(decoder_5_out1), .sel(in_out), .en(_8_out));
  Decoder #(.disabled(0)) decoder_6 (.out0(decoder_6_out0), .out1(decoder_6_out1), .sel(in_out), .en(_10_out));
  assign i_o_data = decoder_6_out1 ? {_3[16], _3[17], _3[18], _3[19], _3[20], _3[21], _3[22], _3[23], _3[24], _3[25], _3[26], _3[27], _3[28], _3[29], _3[30], _3[31]} : 16'bz;  // Controlled_Buffer controlled_buffer_12
  Decoder #(.disabled(0)) decoder_7 (.out0(decoder_7_out0), .out1(decoder_7_out1), .sel(in_out), .en(_12_out));
  Decoder #(.disabled(0)) decoder_8 (.out0(decoder_8_out0), .out1(decoder_8_out1), .sel(in_out), .en(_14_out));
  assign i_o_data = decoder_8_out1 ? {_4[16], _4[17], _4[18], _4[19], _4[20], _4[21], _4[22], _4[23], _4[24], _4[25], _4[26], _4[27], _4[28], _4[29], _4[30], _4[31]} : 16'bz;  // Controlled_Buffer controlled_buffer_13
  Decoder #(.disabled(0)) decoder_9 (.out0(decoder_9_out0), .out1(decoder_9_out1), .sel(in_out), .en(_16_out));
  Decoder #(.disabled(0)) decoder_10 (.out0(decoder_10_out0), .out1(decoder_10_out1), .sel(in_out), .en(_18_out));
  assign i_o_data = decoder_10_out1 ? {_5[16], _5[17], _5[18], _5[19], _5[20], _5[21], _5[22], _5[23], _5[24], _5[25], _5[26], _5[27], _5[28], _5[29], _5[30], _5[31]} : 16'bz;  // Controlled_Buffer controlled_buffer_14
  Decoder #(.disabled(0)) decoder_11 (.out0(decoder_11_out0), .out1(decoder_11_out1), .sel(in_out), .en(_20_out));
  Decoder #(.disabled(0)) decoder_12 (.out0(decoder_12_out0), .out1(decoder_12_out1), .sel(in_out), .en(_22_out));
  assign i_o_data = decoder_12_out1 ? {_6[16], _6[17], _6[18], _6[19], _6[20], _6[21], _6[22], _6[23], _6[24], _6[25], _6[26], _6[27], _6[28], _6[29], _6[30], _6[31]} : 16'bz;  // Controlled_Buffer controlled_buffer_15
  Decoder #(.disabled(0)) decoder_13 (.out0(decoder_13_out0), .out1(decoder_13_out1), .sel(in_out), .en(_24_out));
  Decoder #(.disabled(0)) decoder_14 (.out0(decoder_14_out0), .out1(decoder_14_out1), .sel(in_out), .en(_26_out));
  assign i_o_data = decoder_14_out1 ? {_7[16], _7[17], _7[18], _7[19], _7[20], _7[21], _7[22], _7[23], _7[24], _7[25], _7[26], _7[27], _7[28], _7[29], _7[30], _7[31]} : 16'bz;  // Controlled_Buffer controlled_buffer_16
  Decoder #(.disabled(0)) decoder_15 (.out0(decoder_15_out0), .out1(decoder_15_out1), .sel(in_out), .en(_28_out));
  Decoder #(.disabled(0)) decoder_16 (.out0(decoder_16_out0), .out1(decoder_16_out1), .sel(in_out), .en(_30_out));
  assign i_o_data = decoder_16_out1 ? {_8[16], _8[17], _8[18], _8[19], _8[20], _8[21], _8[22], _8[23], _8[24], _8[25], _8[26], _8[27], _8[28], _8[29], _8[30], _8[31]} : 16'bz;  // Controlled_Buffer controlled_buffer_17
  Decoder #(.disabled(0)) decoder_17 (.out0(decoder_17_out0), .out1(decoder_17_out1), .sel(in_out), .en(_32_out));
  Decoder #(.disabled(0)) decoder_18 (.out0(decoder_18_out0), .out1(decoder_18_out1), .sel(in_out), .en(_34_out));
  assign i_o_data = decoder_18_out1 ? {_9[16], _9[17], _9[18], _9[19], _9[20], _9[21], _9[22], _9[23], _9[24], _9[25], _9[26], _9[27], _9[28], _9[29], _9[30], _9[31]} : 16'bz;  // Controlled_Buffer controlled_buffer_18
  and _0 (_0_out, i_o_sel, comparator_1_eq);
  and u__2 (_2_out, i_o_sel, comparator_2_eq);
  and u__4 (_4_out, i_o_sel, comparator_3_eq);
  and u__6 (_6_out, i_o_sel, comparator_4_eq);
  and u__8 (_8_out, i_o_sel, comparator_5_eq);
  and u__10 (_10_out, i_o_sel, comparator_6_eq);
  and u__12 (_12_out, i_o_sel, comparator_7_eq);
  and u__14 (_14_out, i_o_sel, comparator_8_eq);
  and u__16 (_16_out, i_o_sel, comparator_9_eq);
  and u__18 (_18_out, i_o_sel, comparator_10_eq);
  and u__20 (_20_out, i_o_sel, comparator_11_eq);
  and u__22 (_22_out, i_o_sel, comparator_12_eq);
  and u__24 (_24_out, i_o_sel, comparator_13_eq);
  and u__26 (_26_out, i_o_sel, comparator_14_eq);
  and u__28 (_28_out, i_o_sel, comparator_15_eq);
  and u__30 (_30_out, i_o_sel, comparator_16_eq);
  and u__32 (_32_out, i_o_sel, comparator_17_eq);
  and _34 (_34_out, i_o_sel, comparator_18_eq);
  or or_1 (reset, reset_bird, reset_all);
  Comparator #(.mode("unsigned")) comparator_1 (.a(i_o_adress), .b({8{1'b0}}), .eq(comparator_1_eq));  // open: gt, lt
  Comparator #(.mode("unsigned")) comparator_2 (.a(i_o_adress), .b(8'h2), .eq(comparator_2_eq));  // open: gt, lt
  Comparator #(.mode("unsigned")) comparator_3 (.a(i_o_adress), .b(8'h4), .eq(comparator_3_eq));  // open: gt, lt
  Comparator #(.mode("unsigned")) comparator_4 (.a(i_o_adress), .b(8'h6), .eq(comparator_4_eq));  // open: gt, lt
  Comparator #(.mode("unsigned")) comparator_5 (.a(i_o_adress), .b(8'h8), .eq(comparator_5_eq));  // open: gt, lt
  Comparator #(.mode("unsigned")) comparator_6 (.a(i_o_adress), .b(8'ha), .eq(comparator_6_eq));  // open: gt, lt
  Comparator #(.mode("unsigned")) comparator_7 (.a(i_o_adress), .b(8'hc), .eq(comparator_7_eq));  // open: gt, lt
  Comparator #(.mode("unsigned")) comparator_8 (.a(i_o_adress), .b(8'he), .eq(comparator_8_eq));  // open: gt, lt
  Comparator #(.mode("unsigned")) comparator_9 (.a(i_o_adress), .b(8'h10), .eq(comparator_9_eq));  // open: gt, lt
  Comparator #(.mode("unsigned")) comparator_10 (.a(i_o_adress), .b(8'h12), .eq(comparator_10_eq));  // open: gt, lt
  Comparator #(.mode("unsigned")) comparator_11 (.a(i_o_adress), .b(8'h14), .eq(comparator_11_eq));  // open: gt, lt
  Comparator #(.mode("unsigned")) comparator_12 (.a(i_o_adress), .b(8'h16), .eq(comparator_12_eq));  // open: gt, lt
  Comparator #(.mode("unsigned")) comparator_13 (.a(i_o_adress), .b(8'h18), .eq(comparator_13_eq));  // open: gt, lt
  Comparator #(.mode("unsigned")) comparator_14 (.a(i_o_adress), .b(8'h1a), .eq(comparator_14_eq));  // open: gt, lt
  Comparator #(.mode("unsigned")) comparator_15 (.a(i_o_adress), .b(8'h1c), .eq(comparator_15_eq));  // open: gt, lt
  Comparator #(.mode("unsigned")) comparator_16 (.a(i_o_adress), .b(8'h1e), .eq(comparator_16_eq));  // open: gt, lt
  Comparator #(.mode("unsigned")) comparator_17 (.a(i_o_adress), .b(8'h20), .eq(comparator_17_eq));  // open: gt, lt
  Comparator #(.mode("unsigned")) comparator_18 (.a(i_o_adress), .b(8'h22), .eq(comparator_18_eq));  // open: gt, lt
  assign i_o_data_out = in_out ? i_o_data : 16'bz;  // Controlled_Buffer controlled_buffer_19
  Register #(.width(16)) register_19 (
    .D(i_o_data),
    .Q({_18[0], _18[1], _18[2], _18[3], _18[4], _18[5], _18[6], _18[7], _18[8], _18[9], _18[10], _18[11], _18[12], _18[13], _18[14], _18[15]}),
    .clk(decoder_19_out0), .clr(reset));  // open: en
  Register #(.width(16)) register_20 (
    .D(i_o_data),
    .Q({_18[16], _18[17], _18[18], _18[19], _18[20], _18[21], _18[22], _18[23], _18[24], _18[25], _18[26], _18[27], _18[28], _18[29], _18[30], _18[31]}),
    .clk(decoder_20_out0), .clr(reset));  // open: en
  Register #(.width(16)) register_21 (
    .D(i_o_data),
    .Q({_17[0], _17[1], _17[2], _17[3], _17[4], _17[5], _17[6], _17[7], _17[8], _17[9], _17[10], _17[11], _17[12], _17[13], _17[14], _17[15]}),
    .clk(decoder_21_out0), .clr(reset));  // open: en
  Register #(.width(16)) register_22 (
    .D(i_o_data),
    .Q({_17[16], _17[17], _17[18], _17[19], _17[20], _17[21], _17[22], _17[23], _17[24], _17[25], _17[26], _17[27], _17[28], _17[29], _17[30], _17[31]}),
    .clk(decoder_22_out0), .clr(reset));  // open: en
  Register #(.width(16)) register_23 (
    .D(i_o_data),
    .Q({_16[0], _16[1], _16[2], _16[3], _16[4], _16[5], _16[6], _16[7], _16[8], _16[9], _16[10], _16[11], _16[12], _16[13], _16[14], _16[15]}),
    .clk(decoder_23_out0), .clr(reset));  // open: en
  Register #(.width(16)) register_24 (
    .D(i_o_data),
    .Q({_16[16], _16[17], _16[18], _16[19], _16[20], _16[21], _16[22], _16[23], _16[24], _16[25], _16[26], _16[27], _16[28], _16[29], _16[30], _16[31]}),
    .clk(decoder_24_out0), .clr(reset));  // open: en
  Register #(.width(16)) register_25 (
    .D(i_o_data),
    .Q({_15[0], _15[1], _15[2], _15[3], _15[4], _15[5], _15[6], _15[7], _15[8], _15[9], _15[10], _15[11], _15[12], _15[13], _15[14], _15[15]}),
    .clk(decoder_25_out0), .clr(reset));  // open: en
  Register #(.width(16)) register_26 (
    .D(i_o_data),
    .Q({_15[16], _15[17], _15[18], _15[19], _15[20], _15[21], _15[22], _15[23], _15[24], _15[25], _15[26], _15[27], _15[28], _15[29], _15[30], _15[31]}),
    .clk(decoder_26_out0), .clr(reset));  // open: en
  Register #(.width(16)) register_27 (
    .D(i_o_data),
    .Q({_14[0], _14[1], _14[2], _14[3], _14[4], _14[5], _14[6], _14[7], _14[8], _14[9], _14[10], _14[11], _14[12], _14[13], _14[14], _14[15]}),
    .clk(decoder_27_out0), .clr(reset));  // open: en
  Register #(.width(16)) register_28 (
    .D(i_o_data),
    .Q({_14[16], _14[17], _14[18], _14[19], _14[20], _14[21], _14[22], _14[23], _14[24], _14[25], _14[26], _14[27], _14[28], _14[29], _14[30], _14[31]}),
    .clk(decoder_28_out0), .clr(reset));  // open: en
  Register #(.width(16)) register_29 (
    .D(i_o_data),
    .Q({_13[0], _13[1], _13[2], _13[3], _13[4], _13[5], _13[6], _13[7], _13[8], _13[9], _13[10], _13[11], _13[12], _13[13], _13[14], _13[15]}),
    .clk(decoder_29_out0), .clr(reset));  // open: en
  Register #(.width(16)) register_30 (
    .D(i_o_data),
    .Q({_13[16], _13[17], _13[18], _13[19], _13[20], _13[21], _13[22], _13[23], _13[24], _13[25], _13[26], _13[27], _13[28], _13[29], _13[30], _13[31]}),
    .clk(decoder_30_out0), .clr(reset));  // open: en
  Register #(.width(16)) register_31 (
    .D(i_o_data),
    .Q({_12[0], _12[1], _12[2], _12[3], _12[4], _12[5], _12[6], _12[7], _12[8], _12[9], _12[10], _12[11], _12[12], _12[13], _12[14], _12[15]}),
    .clk(decoder_31_out0), .clr(reset));  // open: en
  Register #(.width(16)) register_32 (
    .D(i_o_data),
    .Q({_12[16], _12[17], _12[18], _12[19], _12[20], _12[21], _12[22], _12[23], _12[24], _12[25], _12[26], _12[27], _12[28], _12[29], _12[30], _12[31]}),
    .clk(decoder_32_out0), .clr(reset));  // open: en
  Register #(.width(16)) register_33 (
    .D(i_o_data),
    .Q({_11[0], _11[1], _11[2], _11[3], _11[4], _11[5], _11[6], _11[7], _11[8], _11[9], _11[10], _11[11], _11[12], _11[13], _11[14], _11[15]}),
    .clk(decoder_33_out0), .clr(reset));  // open: en
  Register #(.width(16)) register_34 (
    .D(i_o_data),
    .Q({_11[16], _11[17], _11[18], _11[19], _11[20], _11[21], _11[22], _11[23], _11[24], _11[25], _11[26], _11[27], _11[28], _11[29], _11[30], _11[31]}),
    .clk(decoder_34_out0), .clr(reset));  // open: en
  Register #(.width(16)) register_35 (
    .D(i_o_data),
    .Q({_10[0], _10[1], _10[2], _10[3], _10[4], _10[5], _10[6], _10[7], _10[8], _10[9], _10[10], _10[11], _10[12], _10[13], _10[14], _10[15]}),
    .clk(decoder_35_out0), .clr(reset));  // open: en
  Register #(.width(16)) register_36 (
    .D(i_o_data),
    .Q({_10[16], _10[17], _10[18], _10[19], _10[20], _10[21], _10[22], _10[23], _10[24], _10[25], _10[26], _10[27], _10[28], _10[29], _10[30], _10[31]}),
    .clk(decoder_36_out0), .clr(reset));  // open: en
  assign i_o_data = decoder_19_out1 ? {_18[0], _18[1], _18[2], _18[3], _18[4], _18[5], _18[6], _18[7], _18[8], _18[9], _18[10], _18[11], _18[12], _18[13], _18[14], _18[15]} : 16'bz;  // Controlled_Buffer controlled_buffer_20
  assign i_o_data = decoder_20_out1 ? {_18[16], _18[17], _18[18], _18[19], _18[20], _18[21], _18[22], _18[23], _18[24], _18[25], _18[26], _18[27], _18[28], _18[29], _18[30], _18[31]} : 16'bz;  // Controlled_Buffer controlled_buffer_21
  assign i_o_data = decoder_21_out1 ? {_17[0], _17[1], _17[2], _17[3], _17[4], _17[5], _17[6], _17[7], _17[8], _17[9], _17[10], _17[11], _17[12], _17[13], _17[14], _17[15]} : 16'bz;  // Controlled_Buffer controlled_buffer_22
  assign i_o_data = decoder_22_out1 ? {_17[16], _17[17], _17[18], _17[19], _17[20], _17[21], _17[22], _17[23], _17[24], _17[25], _17[26], _17[27], _17[28], _17[29], _17[30], _17[31]} : 16'bz;  // Controlled_Buffer controlled_buffer_23
  assign i_o_data = decoder_23_out1 ? {_16[0], _16[1], _16[2], _16[3], _16[4], _16[5], _16[6], _16[7], _16[8], _16[9], _16[10], _16[11], _16[12], _16[13], _16[14], _16[15]} : 16'bz;  // Controlled_Buffer controlled_buffer_24
  assign i_o_data = decoder_24_out1 ? {_16[16], _16[17], _16[18], _16[19], _16[20], _16[21], _16[22], _16[23], _16[24], _16[25], _16[26], _16[27], _16[28], _16[29], _16[30], _16[31]} : 16'bz;  // Controlled_Buffer controlled_buffer_25
  assign i_o_data = decoder_25_out1 ? {_15[0], _15[1], _15[2], _15[3], _15[4], _15[5], _15[6], _15[7], _15[8], _15[9], _15[10], _15[11], _15[12], _15[13], _15[14], _15[15]} : 16'bz;  // Controlled_Buffer controlled_buffer_26
  assign i_o_data = decoder_26_out1 ? {_15[16], _15[17], _15[18], _15[19], _15[20], _15[21], _15[22], _15[23], _15[24], _15[25], _15[26], _15[27], _15[28], _15[29], _15[30], _15[31]} : 16'bz;  // Controlled_Buffer controlled_buffer_27
  assign i_o_data = decoder_27_out1 ? {_14[0], _14[1], _14[2], _14[3], _14[4], _14[5], _14[6], _14[7], _14[8], _14[9], _14[10], _14[11], _14[12], _14[13], _14[14], _14[15]} : 16'bz;  // Controlled_Buffer controlled_buffer_28
  assign i_o_data = decoder_28_out1 ? {_14[16], _14[17], _14[18], _14[19], _14[20], _14[21], _14[22], _14[23], _14[24], _14[25], _14[26], _14[27], _14[28], _14[29], _14[30], _14[31]} : 16'bz;  // Controlled_Buffer controlled_buffer_29
  assign i_o_data = decoder_29_out1 ? {_13[0], _13[1], _13[2], _13[3], _13[4], _13[5], _13[6], _13[7], _13[8], _13[9], _13[10], _13[11], _13[12], _13[13], _13[14], _13[15]} : 16'bz;  // Controlled_Buffer controlled_buffer_30
  assign i_o_data = decoder_30_out1 ? {_13[16], _13[17], _13[18], _13[19], _13[20], _13[21], _13[22], _13[23], _13[24], _13[25], _13[26], _13[27], _13[28], _13[29], _13[30], _13[31]} : 16'bz;  // Controlled_Buffer controlled_buffer_31
  assign i_o_data = decoder_31_out1 ? {_12[0], _12[1], _12[2], _12[3], _12[4], _12[5], _12[6], _12[7], _12[8], _12[9], _12[10], _12[11], _12[12], _12[13], _12[14], _12[15]} : 16'bz;  // Controlled_Buffer controlled_buffer_32
  assign i_o_data = decoder_32_out1 ? {_12[16], _12[17], _12[18], _12[19], _12[20], _12[21], _12[22], _12[23], _12[24], _12[25], _12[26], _12[27], _12[28], _12[29], _12[30], _12[31]} : 16'bz;  // Controlled_Buffer controlled_buffer_33
  assign i_o_data = decoder_33_out1 ? {_11[0], _11[1], _11[2], _11[3], _11[4], _11[5], _11[6], _11[7], _11[8], _11[9], _11[10], _11[11], _11[12], _11[13], _11[14], _11[15]} : 16'bz;  // Controlled_Buffer controlled_buffer_34
  assign i_o_data = decoder_34_out1 ? {_11[16], _11[17], _11[18], _11[19], _11[20], _11[21], _11[22], _11[23], _11[24], _11[25], _11[26], _11[27], _11[28], _11[29], _11[30], _11[31]} : 16'bz;  // Controlled_Buffer controlled_buffer_35
  assign i_o_data = decoder_35_out1 ? {_10[0], _10[1], _10[2], _10[3], _10[4], _10[5], _10[6], _10[7], _10[8], _10[9], _10[10], _10[11], _10[12], _10[13], _10[14], _10[15]} : 16'bz;  // Controlled_Buffer controlled_buffer_36
  assign i_o_data = decoder_36_out1 ? {_10[16], _10[17], _10[18], _10[19], _10[20], _10[21], _10[22], _10[23], _10[24], _10[25], _10[26], _10[27], _10[28], _10[29], _10[30], _10[31]} : 16'bz;  // Controlled_Buffer controlled_buffer_37
  and _68 (_68_out, i_o_sel, comparator_19_eq);
  Decoder #(.disabled(0)) decoder_19 (.out0(decoder_19_out0), .out1(decoder_19_out1), .sel(in_out), .en(_68_out));
  and _70 (_70_out, i_o_sel, comparator_20_eq);
  Decoder #(.disabled(0)) decoder_20 (.out0(decoder_20_out0), .out1(decoder_20_out1), .sel(in_out), .en(_70_out));
  and _64 (_64_out, i_o_sel, comparator_21_eq);
  Decoder #(.disabled(0)) decoder_21 (.out0(decoder_21_out0), .out1(decoder_21_out1), .sel(in_out), .en(_64_out));
  and _66 (_66_out, i_o_sel, comparator_22_eq);
  Decoder #(.disabled(0)) decoder_22 (.out0(decoder_22_out0), .out1(decoder_22_out1), .sel(in_out), .en(_66_out));
  and _60 (_60_out, i_o_sel, comparator_23_eq);
  Decoder #(.disabled(0)) decoder_23 (.out0(decoder_23_out0), .out1(decoder_23_out1), .sel(in_out), .en(_60_out));
  and _62 (_62_out, i_o_sel, comparator_24_eq);
  Decoder #(.disabled(0)) decoder_24 (.out0(decoder_24_out0), .out1(decoder_24_out1), .sel(in_out), .en(_62_out));
  and _56 (_56_out, i_o_sel, comparator_25_eq);
  Decoder #(.disabled(0)) decoder_25 (.out0(decoder_25_out0), .out1(decoder_25_out1), .sel(in_out), .en(_56_out));
  and _58 (_58_out, i_o_sel, comparator_26_eq);
  Decoder #(.disabled(0)) decoder_26 (.out0(decoder_26_out0), .out1(decoder_26_out1), .sel(in_out), .en(_58_out));
  and _52 (_52_out, i_o_sel, comparator_27_eq);
  Decoder #(.disabled(0)) decoder_27 (.out0(decoder_27_out0), .out1(decoder_27_out1), .sel(in_out), .en(_52_out));
  and _54 (_54_out, i_o_sel, comparator_28_eq);
  Decoder #(.disabled(0)) decoder_28 (.out0(decoder_28_out0), .out1(decoder_28_out1), .sel(in_out), .en(_54_out));
  and _48 (_48_out, i_o_sel, comparator_29_eq);
  Decoder #(.disabled(0)) decoder_29 (.out0(decoder_29_out0), .out1(decoder_29_out1), .sel(in_out), .en(_48_out));
  and _50 (_50_out, i_o_sel, comparator_30_eq);
  Decoder #(.disabled(0)) decoder_30 (.out0(decoder_30_out0), .out1(decoder_30_out1), .sel(in_out), .en(_50_out));
  and _44 (_44_out, i_o_sel, comparator_31_eq);
  Decoder #(.disabled(0)) decoder_31 (.out0(decoder_31_out0), .out1(decoder_31_out1), .sel(in_out), .en(_44_out));
  and _46 (_46_out, i_o_sel, comparator_32_eq);
  Decoder #(.disabled(0)) decoder_32 (.out0(decoder_32_out0), .out1(decoder_32_out1), .sel(in_out), .en(_46_out));
  and _40 (_40_out, i_o_sel, comparator_33_eq);
  Decoder #(.disabled(0)) decoder_33 (.out0(decoder_33_out0), .out1(decoder_33_out1), .sel(in_out), .en(_40_out));
  and _42 (_42_out, i_o_sel, comparator_34_eq);
  Decoder #(.disabled(0)) decoder_34 (.out0(decoder_34_out0), .out1(decoder_34_out1), .sel(in_out), .en(_42_out));
  and _36 (_36_out, i_o_sel, comparator_35_eq);
  Decoder #(.disabled(0)) decoder_35 (.out0(decoder_35_out0), .out1(decoder_35_out1), .sel(in_out), .en(_36_out));
  and _38 (_38_out, i_o_sel, comparator_36_eq);
  Decoder #(.disabled(0)) decoder_36 (.out0(decoder_36_out0), .out1(decoder_36_out1), .sel(in_out), .en(_38_out));
  Comparator #(.mode("unsigned")) comparator_19 (.a(i_o_adress), .b(8'h44), .eq(comparator_19_eq));  // open: gt, lt
  Comparator #(.mode("unsigned")) comparator_20 (.a(i_o_adress), .b(8'h46), .eq(comparator_20_eq));  // open: gt, lt
  Comparator #(.mode("unsigned")) comparator_21 (.a(i_o_adress), .b(8'h40), .eq(comparator_21_eq));  // open: gt, lt
  Comparator #(.mode("unsigned")) comparator_22 (.a(i_o_adress), .b(8'h42), .eq(comparator_22_eq));  // open: gt, lt
  Comparator #(.mode("unsigned")) comparator_23 (.a(i_o_adress), .b(8'h3c), .eq(comparator_23_eq));  // open: gt, lt
  Comparator #(.mode("unsigned")) comparator_24 (.a(i_o_adress), .b(8'h3e), .eq(comparator_24_eq));  // open: gt, lt
  Comparator #(.mode("unsigned")) comparator_25 (.a(i_o_adress), .b(8'h38), .eq(comparator_25_eq));  // open: gt, lt
  Comparator #(.mode("unsigned")) comparator_26 (.a(i_o_adress), .b(8'h3a), .eq(comparator_26_eq));  // open: gt, lt
  Comparator #(.mode("unsigned")) comparator_27 (.a(i_o_adress), .b(8'h34), .eq(comparator_27_eq));  // open: gt, lt
  Comparator #(.mode("unsigned")) comparator_28 (.a(i_o_adress), .b(8'h36), .eq(comparator_28_eq));  // open: gt, lt
  Comparator #(.mode("unsigned")) comparator_29 (.a(i_o_adress), .b(8'h30), .eq(comparator_29_eq));  // open: gt, lt
  Comparator #(.mode("unsigned")) comparator_30 (.a(i_o_adress), .b(8'h32), .eq(comparator_30_eq));  // open: gt, lt
  Comparator #(.mode("unsigned")) comparator_31 (.a(i_o_adress), .b(8'h2c), .eq(comparator_31_eq));  // open: gt, lt
  Comparator #(.mode("unsigned")) comparator_32 (.a(i_o_adress), .b(8'h2e), .eq(comparator_32_eq));  // open: gt, lt
  Comparator #(.mode("unsigned")) comparator_33 (.a(i_o_adress), .b(8'h28), .eq(comparator_33_eq));  // open: gt, lt
  Comparator #(.mode("unsigned")) comparator_34 (.a(i_o_adress), .b(8'h2a), .eq(comparator_34_eq));  // open: gt, lt
  Comparator #(.mode("unsigned")) comparator_35 (.a(i_o_adress), .b(8'h24), .eq(comparator_35_eq));  // open: gt, lt
  Comparator #(.mode("unsigned")) comparator_36 (.a(i_o_adress), .b(8'h26), .eq(comparator_36_eq));  // open: gt, lt
  Register #(.width(16)) register_37 (
    .D(i_o_data),
    .Q({_19[0], _19[1], _19[2], _19[3], _19[4], _19[5], _19[6], _19[7], _19[8], _19[9], _19[10], _19[11], _19[12], _19[13], _19[14], _19[15]}),
    .clk(decoder_37_out0), .clr(reset));  // open: en
  Register #(.width(16)) register_38 (
    .D(i_o_data),
    .Q({_19[16], _19[17], _19[18], _19[19], _19[20], _19[21], _19[22], _19[23], _19[24], _19[25], _19[26], _19[27], _19[28], _19[29], _19[30], _19[31]}),
    .clk(decoder_38_out0), .clr(reset));  // open: en
  Register #(.width(16)) register_39 (
    .D(i_o_data),
    .Q({_20[0], _20[1], _20[2], _20[3], _20[4], _20[5], _20[6], _20[7], _20[8], _20[9], _20[10], _20[11], _20[12], _20[13], _20[14], _20[15]}),
    .clk(decoder_39_out0), .clr(reset));  // open: en
  Register #(.width(16)) register_40 (
    .D(i_o_data),
    .Q({_20[16], _20[17], _20[18], _20[19], _20[20], _20[21], _20[22], _20[23], _20[24], _20[25], _20[26], _20[27], _20[28], _20[29], _20[30], _20[31]}),
    .clk(decoder_40_out0), .clr(reset));  // open: en
  Register #(.width(16)) register_41 (
    .D(i_o_data),
    .Q({_21[0], _21[1], _21[2], _21[3], _21[4], _21[5], _21[6], _21[7], _21[8], _21[9], _21[10], _21[11], _21[12], _21[13], _21[14], _21[15]}),
    .clk(decoder_41_out0), .clr(reset));  // open: en
  Register #(.width(16)) register_42 (
    .D(i_o_data),
    .Q({_21[16], _21[17], _21[18], _21[19], _21[20], _21[21], _21[22], _21[23], _21[24], _21[25], _21[26], _21[27], _21[28], _21[29], _21[30], _21[31]}),
    .clk(decoder_42_out0), .clr(reset));  // open: en
  Register #(.width(16)) register_43 (
    .D(i_o_data),
    .Q({_22[0], _22[1], _22[2], _22[3], _22[4], _22[5], _22[6], _22[7], _22[8], _22[9], _22[10], _22[11], _22[12], _22[13], _22[14], _22[15]}),
    .clk(decoder_43_out0), .clr(reset));  // open: en
  Register #(.width(16)) register_44 (
    .D(i_o_data),
    .Q({_22[16], _22[17], _22[18], _22[19], _22[20], _22[21], _22[22], _22[23], _22[24], _22[25], _22[26], _22[27], _22[28], _22[29], _22[30], _22[31]}),
    .clk(decoder_44_out0), .clr(reset));  // open: en
  Register #(.width(16)) register_45 (
    .D(i_o_data),
    .Q({_23[0], _23[1], _23[2], _23[3], _23[4], _23[5], _23[6], _23[7], _23[8], _23[9], _23[10], _23[11], _23[12], _23[13], _23[14], _23[15]}),
    .clk(decoder_45_out0), .clr(reset));  // open: en
  Register #(.width(16)) register_46 (
    .D(i_o_data),
    .Q({_23[16], _23[17], _23[18], _23[19], _23[20], _23[21], _23[22], _23[23], _23[24], _23[25], _23[26], _23[27], _23[28], _23[29], _23[30], _23[31]}),
    .clk(decoder_46_out0), .clr(reset));  // open: en
  Register #(.width(16)) register_47 (
    .D(i_o_data),
    .Q({_24[0], _24[1], _24[2], _24[3], _24[4], _24[5], _24[6], _24[7], _24[8], _24[9], _24[10], _24[11], _24[12], _24[13], _24[14], _24[15]}),
    .clk(decoder_47_out0), .clr(reset));  // open: en
  Register #(.width(16)) register_48 (
    .D(i_o_data),
    .Q({_24[16], _24[17], _24[18], _24[19], _24[20], _24[21], _24[22], _24[23], _24[24], _24[25], _24[26], _24[27], _24[28], _24[29], _24[30], _24[31]}),
    .clk(decoder_48_out0), .clr(reset));  // open: en
  Register #(.width(16)) register_49 (
    .D(i_o_data),
    .Q({_25[0], _25[1], _25[2], _25[3], _25[4], _25[5], _25[6], _25[7], _25[8], _25[9], _25[10], _25[11], _25[12], _25[13], _25[14], _25[15]}),
    .clk(decoder_49_out0), .clr(reset));  // open: en
  Register #(.width(16)) register_50 (
    .D(i_o_data),
    .Q({_25[16], _25[17], _25[18], _25[19], _25[20], _25[21], _25[22], _25[23], _25[24], _25[25], _25[26], _25[27], _25[28], _25[29], _25[30], _25[31]}),
    .clk(decoder_50_out0), .clr(reset));  // open: en
  Register #(.width(16)) register_51 (
    .D(i_o_data),
    .Q({_26[0], _26[1], _26[2], _26[3], _26[4], _26[5], _26[6], _26[7], _26[8], _26[9], _26[10], _26[11], _26[12], _26[13], _26[14], _26[15]}),
    .clk(decoder_51_out0), .clr(reset));  // open: en
  Register #(.width(16)) register_52 (
    .D(i_o_data),
    .Q({_26[16], _26[17], _26[18], _26[19], _26[20], _26[21], _26[22], _26[23], _26[24], _26[25], _26[26], _26[27], _26[28], _26[29], _26[30], _26[31]}),
    .clk(decoder_52_out0), .clr(reset));  // open: en
  Register #(.width(16)) register_53 (
    .D(i_o_data),
    .Q({_27[0], _27[1], _27[2], _27[3], _27[4], _27[5], _27[6], _27[7], _27[8], _27[9], _27[10], _27[11], _27[12], _27[13], _27[14], _27[15]}),
    .clk(decoder_53_out0), .clr(reset));  // open: en
  Register #(.width(16)) register_54 (
    .D(i_o_data),
    .Q({_27[16], _27[17], _27[18], _27[19], _27[20], _27[21], _27[22], _27[23], _27[24], _27[25], _27[26], _27[27], _27[28], _27[29], _27[30], _27[31]}),
    .clk(decoder_54_out0), .clr(reset));  // open: en
  Register #(.width(16)) register_55 (
    .D(i_o_data),
    .Q({_28[0], _28[1], _28[2], _28[3], _28[4], _28[5], _28[6], _28[7], _28[8], _28[9], _28[10], _28[11], _28[12], _28[13], _28[14], _28[15]}),
    .clk(decoder_55_out0), .clr(reset));  // open: en
  Register #(.width(16)) register_56 (
    .D(i_o_data),
    .Q({_28[16], _28[17], _28[18], _28[19], _28[20], _28[21], _28[22], _28[23], _28[24], _28[25], _28[26], _28[27], _28[28], _28[29], _28[30], _28[31]}),
    .clk(decoder_56_out0), .clr(reset));  // open: en
  assign i_o_data = decoder_37_out1 ? {_19[0], _19[1], _19[2], _19[3], _19[4], _19[5], _19[6], _19[7], _19[8], _19[9], _19[10], _19[11], _19[12], _19[13], _19[14], _19[15]} : 16'bz;  // Controlled_Buffer controlled_buffer_38
  assign i_o_data = decoder_38_out1 ? {_19[16], _19[17], _19[18], _19[19], _19[20], _19[21], _19[22], _19[23], _19[24], _19[25], _19[26], _19[27], _19[28], _19[29], _19[30], _19[31]} : 16'bz;  // Controlled_Buffer controlled_buffer_39
  assign i_o_data = decoder_39_out1 ? {_20[0], _20[1], _20[2], _20[3], _20[4], _20[5], _20[6], _20[7], _20[8], _20[9], _20[10], _20[11], _20[12], _20[13], _20[14], _20[15]} : 16'bz;  // Controlled_Buffer controlled_buffer_40
  assign i_o_data = decoder_40_out1 ? {_20[16], _20[17], _20[18], _20[19], _20[20], _20[21], _20[22], _20[23], _20[24], _20[25], _20[26], _20[27], _20[28], _20[29], _20[30], _20[31]} : 16'bz;  // Controlled_Buffer controlled_buffer_41
  assign i_o_data = decoder_41_out1 ? {_21[0], _21[1], _21[2], _21[3], _21[4], _21[5], _21[6], _21[7], _21[8], _21[9], _21[10], _21[11], _21[12], _21[13], _21[14], _21[15]} : 16'bz;  // Controlled_Buffer controlled_buffer_42
  assign i_o_data = decoder_42_out1 ? {_21[16], _21[17], _21[18], _21[19], _21[20], _21[21], _21[22], _21[23], _21[24], _21[25], _21[26], _21[27], _21[28], _21[29], _21[30], _21[31]} : 16'bz;  // Controlled_Buffer controlled_buffer_43
  assign i_o_data = decoder_43_out1 ? {_22[0], _22[1], _22[2], _22[3], _22[4], _22[5], _22[6], _22[7], _22[8], _22[9], _22[10], _22[11], _22[12], _22[13], _22[14], _22[15]} : 16'bz;  // Controlled_Buffer controlled_buffer_44
  assign i_o_data = decoder_44_out1 ? {_22[16], _22[17], _22[18], _22[19], _22[20], _22[21], _22[22], _22[23], _22[24], _22[25], _22[26], _22[27], _22[28], _22[29], _22[30], _22[31]} : 16'bz;  // Controlled_Buffer controlled_buffer_45
  assign i_o_data = decoder_45_out1 ? {_23[0], _23[1], _23[2], _23[3], _23[4], _23[5], _23[6], _23[7], _23[8], _23[9], _23[10], _23[11], _23[12], _23[13], _23[14], _23[15]} : 16'bz;  // Controlled_Buffer controlled_buffer_46
  assign i_o_data = decoder_46_out1 ? {_23[16], _23[17], _23[18], _23[19], _23[20], _23[21], _23[22], _23[23], _23[24], _23[25], _23[26], _23[27], _23[28], _23[29], _23[30], _23[31]} : 16'bz;  // Controlled_Buffer controlled_buffer_47
  assign i_o_data = decoder_47_out1 ? {_24[0], _24[1], _24[2], _24[3], _24[4], _24[5], _24[6], _24[7], _24[8], _24[9], _24[10], _24[11], _24[12], _24[13], _24[14], _24[15]} : 16'bz;  // Controlled_Buffer controlled_buffer_48
  assign i_o_data = decoder_48_out1 ? {_24[16], _24[17], _24[18], _24[19], _24[20], _24[21], _24[22], _24[23], _24[24], _24[25], _24[26], _24[27], _24[28], _24[29], _24[30], _24[31]} : 16'bz;  // Controlled_Buffer controlled_buffer_49
  assign i_o_data = decoder_49_out1 ? {_25[0], _25[1], _25[2], _25[3], _25[4], _25[5], _25[6], _25[7], _25[8], _25[9], _25[10], _25[11], _25[12], _25[13], _25[14], _25[15]} : 16'bz;  // Controlled_Buffer controlled_buffer_50
  assign i_o_data = decoder_50_out1 ? {_25[16], _25[17], _25[18], _25[19], _25[20], _25[21], _25[22], _25[23], _25[24], _25[25], _25[26], _25[27], _25[28], _25[29], _25[30], _25[31]} : 16'bz;  // Controlled_Buffer controlled_buffer_51
  assign i_o_data = decoder_51_out1 ? {_26[0], _26[1], _26[2], _26[3], _26[4], _26[5], _26[6], _26[7], _26[8], _26[9], _26[10], _26[11], _26[12], _26[13], _26[14], _26[15]} : 16'bz;  // Controlled_Buffer controlled_buffer_52
  assign i_o_data = decoder_52_out1 ? {_26[16], _26[17], _26[18], _26[19], _26[20], _26[21], _26[22], _26[23], _26[24], _26[25], _26[26], _26[27], _26[28], _26[29], _26[30], _26[31]} : 16'bz;  // Controlled_Buffer controlled_buffer_53
  assign i_o_data = decoder_53_out1 ? {_27[0], _27[1], _27[2], _27[3], _27[4], _27[5], _27[6], _27[7], _27[8], _27[9], _27[10], _27[11], _27[12], _27[13], _27[14], _27[15]} : 16'bz;  // Controlled_Buffer controlled_buffer_54
  assign i_o_data = decoder_54_out1 ? {_27[16], _27[17], _27[18], _27[19], _27[20], _27[21], _27[22], _27[23], _27[24], _27[25], _27[26], _27[27], _27[28], _27[29], _27[30], _27[31]} : 16'bz;  // Controlled_Buffer controlled_buffer_55
  assign i_o_data = decoder_55_out1 ? {_28[0], _28[1], _28[2], _28[3], _28[4], _28[5], _28[6], _28[7], _28[8], _28[9], _28[10], _28[11], _28[12], _28[13], _28[14], _28[15]} : 16'bz;  // Controlled_Buffer controlled_buffer_56
  assign i_o_data = decoder_56_out1 ? {_28[16], _28[17], _28[18], _28[19], _28[20], _28[21], _28[22], _28[23], _28[24], _28[25], _28[26], _28[27], _28[28], _28[29], _28[30], _28[31]} : 16'bz;  // Controlled_Buffer controlled_buffer_57
  and _72 (_72_out, i_o_sel, comparator_37_eq);
  Decoder #(.disabled(0)) decoder_37 (.out0(decoder_37_out0), .out1(decoder_37_out1), .sel(in_out), .en(_72_out));
  and _74 (_74_out, i_o_sel, comparator_38_eq);
  Decoder #(.disabled(0)) decoder_38 (.out0(decoder_38_out0), .out1(decoder_38_out1), .sel(in_out), .en(_74_out));
  and _76 (_76_out, i_o_sel, comparator_39_eq);
  Decoder #(.disabled(0)) decoder_39 (.out0(decoder_39_out0), .out1(decoder_39_out1), .sel(in_out), .en(_76_out));
  and _78 (_78_out, i_o_sel, comparator_40_eq);
  Decoder #(.disabled(0)) decoder_40 (.out0(decoder_40_out0), .out1(decoder_40_out1), .sel(in_out), .en(_78_out));
  and _80 (_80_out, i_o_sel, comparator_41_eq);
  Decoder #(.disabled(0)) decoder_41 (.out0(decoder_41_out0), .out1(decoder_41_out1), .sel(in_out), .en(_80_out));
  and _82 (_82_out, i_o_sel, comparator_42_eq);
  Decoder #(.disabled(0)) decoder_42 (.out0(decoder_42_out0), .out1(decoder_42_out1), .sel(in_out), .en(_82_out));
  and _84 (_84_out, i_o_sel, comparator_43_eq);
  Decoder #(.disabled(0)) decoder_43 (.out0(decoder_43_out0), .out1(decoder_43_out1), .sel(in_out), .en(_84_out));
  and _86 (_86_out, i_o_sel, comparator_44_eq);
  Decoder #(.disabled(0)) decoder_44 (.out0(decoder_44_out0), .out1(decoder_44_out1), .sel(in_out), .en(_86_out));
  and _88 (_88_out, i_o_sel, comparator_45_eq);
  Decoder #(.disabled(0)) decoder_45 (.out0(decoder_45_out0), .out1(decoder_45_out1), .sel(in_out), .en(_88_out));
  and _90 (_90_out, i_o_sel, comparator_46_eq);
  Decoder #(.disabled(0)) decoder_46 (.out0(decoder_46_out0), .out1(decoder_46_out1), .sel(in_out), .en(_90_out));
  and _92 (_92_out, i_o_sel, comparator_47_eq);
  Decoder #(.disabled(0)) decoder_47 (.out0(decoder_47_out0), .out1(decoder_47_out1), .sel(in_out), .en(_92_out));
  and _94 (_94_out, i_o_sel, comparator_48_eq);
  Decoder #(.disabled(0)) decoder_48 (.out0(decoder_48_out0), .out1(decoder_48_out1), .sel(in_out), .en(_94_out));
  and _96 (_96_out, i_o_sel, comparator_49_eq);
  Decoder #(.disabled(0)) decoder_49 (.out0(decoder_49_out0), .out1(decoder_49_out1), .sel(in_out), .en(_96_out));
  and _98 (_98_out, i_o_sel, comparator_50_eq);
  Decoder #(.disabled(0)) decoder_50 (.out0(decoder_50_out0), .out1(decoder_50_out1), .sel(in_out), .en(_98_out));
  and _100 (_100_out, i_o_sel, comparator_51_eq);
  Decoder #(.disabled(0)) decoder_51 (.out0(decoder_51_out0), .out1(decoder_51_out1), .sel(in_out), .en(_100_out));
  and _102 (_102_out, i_o_sel, comparator_52_eq);
  Decoder #(.disabled(0)) decoder_52 (.out0(decoder_52_out0), .out1(decoder_52_out1), .sel(in_out), .en(_102_out));
  and _104 (_104_out, i_o_sel, comparator_53_eq);
  Decoder #(.disabled(0)) decoder_53 (.out0(decoder_53_out0), .out1(decoder_53_out1), .sel(in_out), .en(_104_out));
  and _106 (_106_out, i_o_sel, comparator_54_eq);
  Decoder #(.disabled(0)) decoder_54 (.out0(decoder_54_out0), .out1(decoder_54_out1), .sel(in_out), .en(_106_out));
  and _108 (_108_out, i_o_sel, comparator_55_eq);
  Decoder #(.disabled(0)) decoder_55 (.out0(decoder_55_out0), .out1(decoder_55_out1), .sel(in_out), .en(_108_out));
  and _110 (_110_out, i_o_sel, comparator_56_eq);
  Decoder #(.disabled(0)) decoder_56 (.out0(decoder_56_out0), .out1(decoder_56_out1), .sel(in_out), .en(_110_out));
  Comparator #(.mode("unsigned")) comparator_37 (.a(i_o_adress), .b(8'h48), .eq(comparator_37_eq));  // open: gt, lt
  Comparator #(.mode("unsigned")) comparator_38 (.a(i_o_adress), .b(8'h4a), .eq(comparator_38_eq));  // open: gt, lt
  Comparator #(.mode("unsigned")) comparator_39 (.a(i_o_adress), .b(8'h4c), .eq(comparator_39_eq));  // open: gt, lt
  Comparator #(.mode("unsigned")) comparator_40 (.a(i_o_adress), .b(8'h4e), .eq(comparator_40_eq));  // open: gt, lt
  Comparator #(.mode("unsigned")) comparator_41 (.a(i_o_adress), .b(8'h50), .eq(comparator_41_eq));  // open: gt, lt
  Comparator #(.mode("unsigned")) comparator_42 (.a(i_o_adress), .b(8'h52), .eq(comparator_42_eq));  // open: gt, lt
  Comparator #(.mode("unsigned")) comparator_43 (.a(i_o_adress), .b(8'h54), .eq(comparator_43_eq));  // open: gt, lt
  Comparator #(.mode("unsigned")) comparator_44 (.a(i_o_adress), .b(8'h56), .eq(comparator_44_eq));  // open: gt, lt
  Comparator #(.mode("unsigned")) comparator_45 (.a(i_o_adress), .b(8'h58), .eq(comparator_45_eq));  // open: gt, lt
  Comparator #(.mode("unsigned")) comparator_46 (.a(i_o_adress), .b(8'h5a), .eq(comparator_46_eq));  // open: gt, lt
  Comparator #(.mode("unsigned")) comparator_47 (.a(i_o_adress), .b(8'h5c), .eq(comparator_47_eq));  // open: gt, lt
  Comparator #(.mode("unsigned")) comparator_48 (.a(i_o_adress), .b(8'h5e), .eq(comparator_48_eq));  // open: gt, lt
  Comparator #(.mode("unsigned")) comparator_49 (.a(i_o_adress), .b(8'h60), .eq(comparator_49_eq));  // open: gt, lt
  Comparator #(.mode("unsigned")) comparator_50 (.a(i_o_adress), .b(8'h62), .eq(comparator_50_eq));  // open: gt, lt
  Comparator #(.mode("unsigned")) comparator_51 (.a(i_o_adress), .b(8'h64), .eq(comparator_51_eq));  // open: gt, lt
  Comparator #(.mode("unsigned")) comparator_52 (.a(i_o_adress), .b(8'h66), .eq(comparator_52_eq));  // open: gt, lt
  Comparator #(.mode("unsigned")) comparator_53 (.a(i_o_adress), .b(8'h68), .eq(comparator_53_eq));  // open: gt, lt
  Comparator #(.mode("unsigned")) comparator_54 (.a(i_o_adress), .b(8'h6a), .eq(comparator_54_eq));  // open: gt, lt
  Comparator #(.mode("unsigned")) comparator_55 (.a(i_o_adress), .b(8'h6c), .eq(comparator_55_eq));  // open: gt, lt
  Comparator #(.mode("unsigned")) comparator_56 (.a(i_o_adress), .b(8'h6e), .eq(comparator_56_eq));  // open: gt, lt
  Register #(.width(16)) register_57 (
    .D(i_o_data), .Q({register_57_q, \end }), .clk(decoder_57_out0), .clr(reset_all));  // open: en
  Register #(.width(16)) register_58 (
    .D(i_o_data), .Q(birds_flew_away), .clk(decoder_58_out0), .clr(reset_all));  // open: en
  Register #(.width(16)) register_59 (.D(i_o_data), .Q(score), .clk(decoder_59_out0), .clr(reset_all));  // open: en
  Random #(.width(16), .seed(3456)) random_1 (.clk(clock), .out(random_1_out));  // open: next, clr
  Register #(.width(16)) register_60 (
    .D(i_o_data),
    .Q({_32[0], _32[1], _32[2], _32[3], _32[4], _32[5], _32[6], _32[7], _32[8], _32[9], _32[10], _32[11], _32[12], _32[13], _32[14], _32[15]}),
    .clk(decoder_61_out0), .clr(reset));  // open: en
  Register #(.width(16)) register_61 (
    .D(i_o_data),
    .Q({_32[16], _32[17], _32[18], _32[19], _32[20], _32[21], _32[22], _32[23], _32[24], _32[25], _32[26], _32[27], _32[28], _32[29], _32[30], _32[31]}),
    .clk(decoder_62_out0), .clr(reset));  // open: en
  Register #(.width(16)) register_62 (
    .D(i_o_data),
    .Q({_31[0], _31[1], _31[2], _31[3], _31[4], _31[5], _31[6], _31[7], _31[8], _31[9], _31[10], _31[11], _31[12], _31[13], _31[14], _31[15]}),
    .clk(decoder_63_out0), .clr(reset));  // open: en
  Register #(.width(16)) register_63 (
    .D(i_o_data),
    .Q({_31[16], _31[17], _31[18], _31[19], _31[20], _31[21], _31[22], _31[23], _31[24], _31[25], _31[26], _31[27], _31[28], _31[29], _31[30], _31[31]}),
    .clk(decoder_64_out0), .clr(reset));  // open: en
  Register #(.width(16)) register_64 (
    .D(i_o_data),
    .Q({_30[0], _30[1], _30[2], _30[3], _30[4], _30[5], _30[6], _30[7], _30[8], _30[9], _30[10], _30[11], _30[12], _30[13], _30[14], _30[15]}),
    .clk(decoder_65_out0), .clr(reset));  // open: en
  Register #(.width(16)) register_65 (
    .D(i_o_data),
    .Q({_30[16], _30[17], _30[18], _30[19], _30[20], _30[21], _30[22], _30[23], _30[24], _30[25], _30[26], _30[27], _30[28], _30[29], _30[30], _30[31]}),
    .clk(decoder_66_out0), .clr(reset));  // open: en
  Register #(.width(16)) register_66 (
    .D(i_o_data),
    .Q({_29[0], _29[1], _29[2], _29[3], _29[4], _29[5], _29[6], _29[7], _29[8], _29[9], _29[10], _29[11], _29[12], _29[13], _29[14], _29[15]}),
    .clk(decoder_67_out0), .clr(reset));  // open: en
  Register #(.width(16)) register_67 (
    .D(i_o_data),
    .Q({_29[16], _29[17], _29[18], _29[19], _29[20], _29[21], _29[22], _29[23], _29[24], _29[25], _29[26], _29[27], _29[28], _29[29], _29[30], _29[31]}),
    .clk(decoder_68_out0), .clr(reset));  // open: en
  assign i_o_data = decoder_57_out1 ? {register_57_q, \end } : 16'bz;  // Controlled_Buffer controlled_buffer_58
  assign i_o_data = decoder_58_out1 ? birds_flew_away : 16'bz;  // Controlled_Buffer controlled_buffer_59
  assign i_o_data = decoder_59_out1 ? score : 16'bz;  // Controlled_Buffer controlled_buffer_60
  assign i_o_data = decoder_60_out1 ? random_1_out : 16'bz;  // Controlled_Buffer controlled_buffer_61
  assign i_o_data = decoder_61_out1 ? {_32[0], _32[1], _32[2], _32[3], _32[4], _32[5], _32[6], _32[7], _32[8], _32[9], _32[10], _32[11], _32[12], _32[13], _32[14], _32[15]} : 16'bz;  // Controlled_Buffer controlled_buffer_62
  assign i_o_data = decoder_62_out1 ? {_32[16], _32[17], _32[18], _32[19], _32[20], _32[21], _32[22], _32[23], _32[24], _32[25], _32[26], _32[27], _32[28], _32[29], _32[30], _32[31]} : 16'bz;  // Controlled_Buffer controlled_buffer_63
  assign i_o_data = decoder_63_out1 ? {_31[0], _31[1], _31[2], _31[3], _31[4], _31[5], _31[6], _31[7], _31[8], _31[9], _31[10], _31[11], _31[12], _31[13], _31[14], _31[15]} : 16'bz;  // Controlled_Buffer controlled_buffer_64
  assign i_o_data = decoder_64_out1 ? {_31[16], _31[17], _31[18], _31[19], _31[20], _31[21], _31[22], _31[23], _31[24], _31[25], _31[26], _31[27], _31[28], _31[29], _31[30], _31[31]} : 16'bz;  // Controlled_Buffer controlled_buffer_65
  assign i_o_data = decoder_65_out1 ? {_30[0], _30[1], _30[2], _30[3], _30[4], _30[5], _30[6], _30[7], _30[8], _30[9], _30[10], _30[11], _30[12], _30[13], _30[14], _30[15]} : 16'bz;  // Controlled_Buffer controlled_buffer_66
  assign i_o_data = decoder_66_out1 ? {_30[16], _30[17], _30[18], _30[19], _30[20], _30[21], _30[22], _30[23], _30[24], _30[25], _30[26], _30[27], _30[28], _30[29], _30[30], _30[31]} : 16'bz;  // Controlled_Buffer controlled_buffer_67
  assign i_o_data = decoder_67_out1 ? {_29[0], _29[1], _29[2], _29[3], _29[4], _29[5], _29[6], _29[7], _29[8], _29[9], _29[10], _29[11], _29[12], _29[13], _29[14], _29[15]} : 16'bz;  // Controlled_Buffer controlled_buffer_68
  assign i_o_data = decoder_68_out1 ? {_29[16], _29[17], _29[18], _29[19], _29[20], _29[21], _29[22], _29[23], _29[24], _29[25], _29[26], _29[27], _29[28], _29[29], _29[30], _29[31]} : 16'bz;  // Controlled_Buffer controlled_buffer_69
  and _166 (_166_out, i_o_sel, comparator_57_eq);
  Decoder #(.disabled(0)) decoder_57 (.out0(decoder_57_out0), .out1(decoder_57_out1), .sel(in_out), .en(_166_out));
  and _164 (_164_out, i_o_sel, comparator_58_eq);
  Decoder #(.disabled(0)) decoder_58 (.out0(decoder_58_out0), .out1(decoder_58_out1), .sel(in_out), .en(_164_out));
  and _160 (_160_out, i_o_sel, comparator_59_eq);
  Decoder #(.disabled(0)) decoder_59 (.out0(decoder_59_out0), .out1(decoder_59_out1), .sel(in_out), .en(_160_out));
  and _128 (_128_out, i_o_sel, comparator_60_eq);
  Decoder #(.disabled(0)) decoder_60 (.out1(decoder_60_out1), .sel(in_out), .en(_128_out));  // open: out0
  and _124 (_124_out, i_o_sel, comparator_61_eq);
  Decoder #(.disabled(0)) decoder_61 (.out0(decoder_61_out0), .out1(decoder_61_out1), .sel(in_out), .en(_124_out));
  and _126 (_126_out, i_o_sel, comparator_62_eq);
  Decoder #(.disabled(0)) decoder_62 (.out0(decoder_62_out0), .out1(decoder_62_out1), .sel(in_out), .en(_126_out));
  and _120 (_120_out, i_o_sel, comparator_63_eq);
  Decoder #(.disabled(0)) decoder_63 (.out0(decoder_63_out0), .out1(decoder_63_out1), .sel(in_out), .en(_120_out));
  and _122 (_122_out, i_o_sel, comparator_64_eq);
  Decoder #(.disabled(0)) decoder_64 (.out0(decoder_64_out0), .out1(decoder_64_out1), .sel(in_out), .en(_122_out));
  and _116 (_116_out, i_o_sel, comparator_65_eq);
  Decoder #(.disabled(0)) decoder_65 (.out0(decoder_65_out0), .out1(decoder_65_out1), .sel(in_out), .en(_116_out));
  and _118 (_118_out, i_o_sel, comparator_66_eq);
  Decoder #(.disabled(0)) decoder_66 (.out0(decoder_66_out0), .out1(decoder_66_out1), .sel(in_out), .en(_118_out));
  and _112 (_112_out, i_o_sel, comparator_67_eq);
  Decoder #(.disabled(0)) decoder_67 (.out0(decoder_67_out0), .out1(decoder_67_out1), .sel(in_out), .en(_112_out));
  and _114 (_114_out, i_o_sel, comparator_68_eq);
  Decoder #(.disabled(0)) decoder_68 (.out0(decoder_68_out0), .out1(decoder_68_out1), .sel(in_out), .en(_114_out));
  Comparator #(.mode("unsigned")) comparator_57 (.a(i_o_adress), .b(8'ha6), .eq(comparator_57_eq));  // open: gt, lt
  Comparator #(.mode("unsigned")) comparator_58 (.a(i_o_adress), .b(8'ha4), .eq(comparator_58_eq));  // open: gt, lt
  Comparator #(.mode("unsigned")) comparator_59 (.a(i_o_adress), .b(8'ha0), .eq(comparator_59_eq));  // open: gt, lt
  Comparator #(.mode("unsigned")) comparator_60 (.a(i_o_adress), .b(8'h80), .eq(comparator_60_eq));  // open: gt, lt
  Comparator #(.mode("unsigned")) comparator_61 (.a(i_o_adress), .b(8'h7c), .eq(comparator_61_eq));  // open: gt, lt
  Comparator #(.mode("unsigned")) comparator_62 (.a(i_o_adress), .b(8'h7e), .eq(comparator_62_eq));  // open: gt, lt
  Comparator #(.mode("unsigned")) comparator_63 (.a(i_o_adress), .b(8'h78), .eq(comparator_63_eq));  // open: gt, lt
  Comparator #(.mode("unsigned")) comparator_64 (.a(i_o_adress), .b(8'h7a), .eq(comparator_64_eq));  // open: gt, lt
  Comparator #(.mode("unsigned")) comparator_65 (.a(i_o_adress), .b(8'h74), .eq(comparator_65_eq));  // open: gt, lt
  Comparator #(.mode("unsigned")) comparator_66 (.a(i_o_adress), .b(8'h76), .eq(comparator_66_eq));  // open: gt, lt
  Comparator #(.mode("unsigned")) comparator_67 (.a(i_o_adress), .b(8'h70), .eq(comparator_67_eq));  // open: gt, lt
  Comparator #(.mode("unsigned")) comparator_68 (.a(i_o_adress), .b(8'h72), .eq(comparator_68_eq));  // open: gt, lt
endmodule
module gunsight_subsystem (
  input  gunsight_ans,
  input  in_out,
  input  [15:0] i_o_data_control,
  input  i_o_sel,
  input  [7:0] i_o_adress,
  input  keyboard_active,
  input  [6:0] keyboard,
  output [15:0] out,
  output [31:0] _1,
  output [31:0] _19,
  output [31:0] _18,
  output [31:0] _2,
  output [31:0] _20,
  output [31:0] _17,
  output [31:0] _21,
  output [31:0] _16,
  output [31:0] _3,
  output [31:0] _22,
  output [31:0] _15,
  output [31:0] _4,
  output [31:0] _23,
  output [31:0] _14,
  output [31:0] _5,
  output [31:0] _24,
  output [31:0] _13,
  output [31:0] _6,
  output [31:0] _25,
  output [31:0] _32,
  output [31:0] _12,
  output [31:0] _7,
  output [31:0] _26,
  output [31:0] _31,
  output [31:0] _8,
  output [31:0] _11,
  output [31:0] _30,
  output [31:0] _27,
  output [31:0] _10,
  output [31:0] _9,
  output [31:0] _29,
  output [31:0] _28
);

  wire _0_out, _2_out, _4_out, _6_out, _8_out, _10_out, _12_out, _14_out, _16_out, _18_out, _20_out, _22_out,
       _24_out, _26_out, _28_out, _30_out, _32_out, _34_out, _36_out, _38_out, _40_out, _42_out, _44_out,
       _46_out, _48_out, _50_out, _52_out, _54_out, _56_out, _58_out, _60_out, _62_out, _64_out, _66_out,
       _68_out, _70_out, _72_out, _74_out, _76_out, _78_out, _80_out, _82_out, _84_out, _86_out, _88_out,
       _90_out, _92_out, _94_out, _96_out, _98_out, _100_out, _102_out, _104_out, _106_out, _108_out,
       _110_out, _112_out, _114_out, _116_out, _118_out, _120_out, _122_out, _124_out, _126_out, _176_out,
       and_1_out, comparator_1_eq, comparator_2_eq, comparator_3_eq, comparator_4_eq, comparator_5_eq,
       comparator_6_eq, comparator_7_eq, comparator_8_eq, comparator_9_eq, comparator_10_eq,
       comparator_11_eq, comparator_12_eq, comparator_13_eq, comparator_14_eq, comparator_15_eq,
       comparator_16_eq, comparator_17_eq, comparator_18_eq, comparator_19_eq, comparator_20_eq,
       comparator_21_eq, comparator_22_eq, comparator_23_eq, comparator_24_eq, comparator_25_eq,
       comparator_26_eq, comparator_27_eq, comparator_28_eq, comparator_29_eq, comparator_30_eq,
       comparator_31_eq, comparator_32_eq, comparator_33_eq, comparator_34_eq, comparator_35_eq,
       comparator_36_eq, comparator_37_eq, comparator_38_eq, comparator_39_eq, comparator_40_eq,
       comparator_41_eq, comparator_42_eq, comparator_43_eq, comparator_44_eq, comparator_45_eq,
       comparator_46_eq, comparator_47_eq, comparator_48_eq, comparator_49_eq, comparator_50_eq,
       comparator_51_eq, comparator_52_eq, comparator_53_eq, comparator_54_eq, comparator_55_eq,
       comparator_56_eq, comparator_57_eq, comparator_58_eq, comparator_59_eq, comparator_60_eq,
       comparator_61_eq, comparator_62_eq, comparator_63_eq, comparator_64_eq, comparator_65_eq,
       comparator_66_eq, comparator_67_eq, comparator_68_eq, comparator_69_eq, decoder_1_out0,
       decoder_1_out1, decoder_2_out0, decoder_2_out1, decoder_3_out0, decoder_3_out1, decoder_4_out0,
       decoder_4_out1, decoder_5_out0, decoder_5_out1, decoder_6_out0, decoder_6_out1, decoder_7_out0,
       decoder_7_out1, decoder_8_out0, decoder_8_out1, decoder_9_out0, decoder_9_out1, decoder_10_out0,
       decoder_10_out1, decoder_11_out0, decoder_11_out1, decoder_12_out0, decoder_12_out1, decoder_13_out0,
       decoder_13_out1, decoder_14_out0, decoder_14_out1, decoder_15_out0, decoder_15_out1, decoder_16_out0,
       decoder_16_out1, decoder_17_out0, decoder_17_out1, decoder_18_out0, decoder_18_out1, decoder_19_out0,
       decoder_19_out1, decoder_20_out0, decoder_20_out1, decoder_21_out0, decoder_21_out1, decoder_22_out0,
       decoder_22_out1, decoder_23_out0, decoder_23_out1, decoder_24_out0, decoder_24_out1, decoder_25_out0,
       decoder_25_out1, decoder_26_out0, decoder_26_out1, decoder_27_out0, decoder_27_out1, decoder_28_out0,
       decoder_28_out1, decoder_29_out0, decoder_29_out1, decoder_30_out0, decoder_30_out1, decoder_31_out0,
       decoder_31_out1, decoder_32_out0, decoder_32_out1, decoder_33_out0, decoder_33_out1, decoder_34_out0,
       decoder_34_out1, decoder_35_out0, decoder_35_out1, decoder_36_out0, decoder_36_out1, decoder_37_out0,
       decoder_37_out1, decoder_38_out0, decoder_38_out1, decoder_39_out0, decoder_39_out1, decoder_40_out0,
       decoder_40_out1, decoder_41_out0, decoder_41_out1, decoder_42_out0, decoder_42_out1, decoder_43_out0,
       decoder_43_out1, decoder_44_out0, decoder_44_out1, decoder_45_out0, decoder_45_out1, decoder_46_out0,
       decoder_46_out1, decoder_47_out0, decoder_47_out1, decoder_48_out0, decoder_48_out1, decoder_49_out0,
       decoder_49_out1, decoder_50_out0, decoder_50_out1, decoder_51_out0, decoder_51_out1, decoder_52_out0,
       decoder_52_out1, decoder_53_out0, decoder_53_out1, decoder_54_out0, decoder_54_out1, decoder_55_out0,
       decoder_55_out1, decoder_56_out0, decoder_56_out1, decoder_57_out1, decoder_58_out0, decoder_58_out1,
       decoder_59_out0, decoder_59_out1, decoder_60_out0, decoder_60_out1, decoder_61_out0, decoder_61_out1,
       decoder_62_out0, decoder_62_out1, decoder_63_out0, decoder_63_out1, decoder_64_out0, decoder_64_out1,
       decoder_65_out0, decoder_65_out1, nor_1_out, nor_2_out, not_1_out, not_2_out, or_1_out,
       pull_resistor_1_node;
  wire [6:0] register_57_q;
  wire [15:7] s_r_ff_1_q;

  Register #(.width(16)) register_1 (
    .D(i_o_data_control), .Q(_1[15:0]), .clk(decoder_1_out0), .clr(gunsight_ans));  // open: en
  Register #(.width(16)) register_2 (
    .D(i_o_data_control), .Q(_1[31:16]), .clk(decoder_2_out0), .clr(gunsight_ans));  // open: en
  Register #(.width(16)) register_3 (
    .D(i_o_data_control), .Q(_2[15:0]), .clk(decoder_3_out0), .clr(gunsight_ans));  // open: en
  Register #(.width(16)) register_4 (
    .D(i_o_data_control), .Q(_2[31:16]), .clk(decoder_4_out0), .clr(gunsight_ans));  // open: en
  Register #(.width(16)) register_5 (
    .D(i_o_data_control), .Q(_3[15:0]), .clk(decoder_5_out0), .clr(gunsight_ans));  // open: en
  Register #(.width(16)) register_6 (
    .D(i_o_data_control), .Q(_3[31:16]), .clk(decoder_6_out0), .clr(gunsight_ans));  // open: en
  Register #(.width(16)) register_7 (
    .D(i_o_data_control), .Q(_4[15:0]), .clk(decoder_7_out0), .clr(gunsight_ans));  // open: en
  Register #(.width(16)) register_8 (
    .D(i_o_data_control), .Q(_4[31:16]), .clk(decoder_8_out0), .clr(gunsight_ans));  // open: en
  Register #(.width(16)) register_9 (
    .D(i_o_data_control), .Q(_5[15:0]), .clk(decoder_9_out0), .clr(gunsight_ans));  // open: en
  Register #(.width(16)) register_10 (
    .D(i_o_data_control), .Q(_5[31:16]), .clk(decoder_10_out0), .clr(gunsight_ans));  // open: en
  Register #(.width(16)) register_11 (
    .D(i_o_data_control), .Q(_6[15:0]), .clk(decoder_11_out0), .clr(gunsight_ans));  // open: en
  Register #(.width(16)) register_12 (
    .D(i_o_data_control), .Q(_6[31:16]), .clk(decoder_12_out0), .clr(gunsight_ans));  // open: en
  Register #(.width(16)) register_13 (
    .D(i_o_data_control), .Q(_7[15:0]), .clk(decoder_13_out0), .clr(gunsight_ans));  // open: en
  Register #(.width(16)) register_14 (
    .D(i_o_data_control), .Q(_7[31:16]), .clk(decoder_14_out0), .clr(gunsight_ans));  // open: en
  Register #(.width(16)) register_15 (
    .D(i_o_data_control), .Q(_8[15:0]), .clk(decoder_15_out0), .clr(gunsight_ans));  // open: en
  Register #(.width(16)) register_16 (
    .D(i_o_data_control), .Q(_8[31:16]), .clk(decoder_16_out0), .clr(gunsight_ans));  // open: en
  Register #(.width(16)) register_17 (
    .D(i_o_data_control), .Q(_9[15:0]), .clk(decoder_17_out0), .clr(gunsight_ans));  // open: en
  Register #(.width(16)) register_18 (.D(i_o_data_control), .Q(_9[31:16]), .clk(decoder_18_out0));  // open: en, clr
  assign i_o_data_control = decoder_3_out1 ? _2[15:0] : 16'bz;  // Controlled_Buffer controlled_buffer_1
  assign i_o_data_control = decoder_4_out1 ? _2[31:16] : 16'bz;  // Controlled_Buffer controlled_buffer_2
  assign i_o_data_control = decoder_5_out1 ? _3[15:0] : 16'bz;  // Controlled_Buffer controlled_buffer_3
  assign i_o_data_control = decoder_6_out1 ? _3[31:16] : 16'bz;  // Controlled_Buffer controlled_buffer_4
  assign i_o_data_control = decoder_7_out1 ? _4[15:0] : 16'bz;  // Controlled_Buffer controlled_buffer_5
  assign i_o_data_control = decoder_8_out1 ? _4[31:16] : 16'bz;  // Controlled_Buffer controlled_buffer_6
  assign i_o_data_control = decoder_9_out1 ? _5[15:0] : 16'bz;  // Controlled_Buffer controlled_buffer_7
  assign i_o_data_control = decoder_10_out1 ? _5[31:16] : 16'bz;  // Controlled_Buffer controlled_buffer_8
  assign i_o_data_control = decoder_11_out1 ? _6[15:0] : 16'bz;  // Controlled_Buffer controlled_buffer_9
  assign i_o_data_control = decoder_12_out1 ? _6[31:16] : 16'bz;  // Controlled_Buffer controlled_buffer_10
  assign i_o_data_control = decoder_13_out1 ? _7[15:0] : 16'bz;  // Controlled_Buffer controlled_buffer_11
  assign i_o_data_control = decoder_14_out1 ? _7[31:16] : 16'bz;  // Controlled_Buffer controlled_buffer_12
  assign i_o_data_control = decoder_15_out1 ? _8[15:0] : 16'bz;  // Controlled_Buffer controlled_buffer_13
  assign i_o_data_control = decoder_16_out1 ? _8[31:16] : 16'bz;  // Controlled_Buffer controlled_buffer_14
  assign i_o_data_control = decoder_17_out1 ? _9[15:0] : 16'bz;  // Controlled_Buffer controlled_buffer_15
  assign i_o_data_control = decoder_18_out1 ? _9[31:16] : 16'bz;  // Controlled_Buffer controlled_buffer_16
  assign i_o_data_control = decoder_1_out1 ? _1[15:0] : 16'bz;  // Controlled_Buffer controlled_buffer_17
  Decoder #(.disabled(0)) decoder_1 (.out0(decoder_1_out0), .out1(decoder_1_out1), .sel(in_out), .en(_0_out));
  Decoder #(.disabled(0)) decoder_2 (.out0(decoder_2_out0), .out1(decoder_2_out1), .sel(in_out), .en(_2_out));
  assign i_o_data_control = decoder_2_out1 ? _1[31:16] : 16'bz;  // Controlled_Buffer controlled_buffer_18
  and u__4 (_4_out, i_o_sel, comparator_3_eq);
  Decoder #(.disabled(0)) decoder_3 (.out0(decoder_3_out0), .out1(decoder_3_out1), .sel(in_out), .en(_4_out));
  and u__6 (_6_out, i_o_sel, comparator_4_eq);
  Decoder #(.disabled(0)) decoder_4 (.out0(decoder_4_out0), .out1(decoder_4_out1), .sel(in_out), .en(_6_out));
  and u__8 (_8_out, i_o_sel, comparator_5_eq);
  Decoder #(.disabled(0)) decoder_5 (.out0(decoder_5_out0), .out1(decoder_5_out1), .sel(in_out), .en(_8_out));
  and u__10 (_10_out, i_o_sel, comparator_6_eq);
  Decoder #(.disabled(0)) decoder_6 (.out0(decoder_6_out0), .out1(decoder_6_out1), .sel(in_out), .en(_10_out));
  and u__12 (_12_out, i_o_sel, comparator_7_eq);
  Decoder #(.disabled(0)) decoder_7 (.out0(decoder_7_out0), .out1(decoder_7_out1), .sel(in_out), .en(_12_out));
  and u__14 (_14_out, i_o_sel, comparator_8_eq);
  Decoder #(.disabled(0)) decoder_8 (.out0(decoder_8_out0), .out1(decoder_8_out1), .sel(in_out), .en(_14_out));
  and u__16 (_16_out, i_o_sel, comparator_9_eq);
  Decoder #(.disabled(0)) decoder_9 (.out0(decoder_9_out0), .out1(decoder_9_out1), .sel(in_out), .en(_16_out));
  and u__18 (_18_out, i_o_sel, comparator_10_eq);
  Decoder #(.disabled(0)) decoder_10 (.out0(decoder_10_out0), .out1(decoder_10_out1), .sel(in_out), .en(_18_out));
  and u__20 (_20_out, i_o_sel, comparator_11_eq);
  Decoder #(.disabled(0)) decoder_11 (.out0(decoder_11_out0), .out1(decoder_11_out1), .sel(in_out), .en(_20_out));
  and u__22 (_22_out, i_o_sel, comparator_12_eq);
  Decoder #(.disabled(0)) decoder_12 (.out0(decoder_12_out0), .out1(decoder_12_out1), .sel(in_out), .en(_22_out));
  and u__24 (_24_out, i_o_sel, comparator_13_eq);
  Decoder #(.disabled(0)) decoder_13 (.out0(decoder_13_out0), .out1(decoder_13_out1), .sel(in_out), .en(_24_out));
  and u__26 (_26_out, i_o_sel, comparator_14_eq);
  Decoder #(.disabled(0)) decoder_14 (.out0(decoder_14_out0), .out1(decoder_14_out1), .sel(in_out), .en(_26_out));
  and u__28 (_28_out, i_o_sel, comparator_15_eq);
  Decoder #(.disabled(0)) decoder_15 (.out0(decoder_15_out0), .out1(decoder_15_out1), .sel(in_out), .en(_28_out));
  and u__30 (_30_out, i_o_sel, comparator_16_eq);
  Decoder #(.disabled(0)) decoder_16 (.out0(decoder_16_out0), .out1(decoder_16_out1), .sel(in_out), .en(_30_out));
  and u__32 (_32_out, i_o_sel, comparator_17_eq);
  Decoder #(.disabled(0)) decoder_17 (.out0(decoder_17_out0), .out1(decoder_17_out1), .sel(in_out), .en(_32_out));
  and _34 (_34_out, i_o_sel, comparator_18_eq);
  Decoder #(.disabled(0)) decoder_18 (.out0(decoder_18_out0), .out1(decoder_18_out1), .sel(in_out), .en(_34_out));
  and _0 (_0_out, i_o_sel, comparator_1_eq);
  and u__2 (_2_out, i_o_sel, comparator_2_eq);
  Comparator #(.mode("unsigned")) comparator_1 (.a(i_o_adress), .b({8{1'b0}}), .eq(comparator_1_eq));  // open: gt, lt
  Comparator #(.mode("unsigned")) comparator_2 (.a(i_o_adress), .b(8'h2), .eq(comparator_2_eq));  // open: gt, lt
  Comparator #(.mode("unsigned")) comparator_3 (.a(i_o_adress), .b(8'h4), .eq(comparator_3_eq));  // open: gt, lt
  Comparator #(.mode("unsigned")) comparator_4 (.a(i_o_adress), .b(8'h6), .eq(comparator_4_eq));  // open: gt, lt
  Comparator #(.mode("unsigned")) comparator_5 (.a(i_o_adress), .b(8'h8), .eq(comparator_5_eq));  // open: gt, lt
  Comparator #(.mode("unsigned")) comparator_6 (.a(i_o_adress), .b(8'ha), .eq(comparator_6_eq));  // open: gt, lt
  Comparator #(.mode("unsigned")) comparator_7 (.a(i_o_adress), .b(8'hc), .eq(comparator_7_eq));  // open: gt, lt
  Comparator #(.mode("unsigned")) comparator_8 (.a(i_o_adress), .b(8'he), .eq(comparator_8_eq));  // open: gt, lt
  Comparator #(.mode("unsigned")) comparator_9 (.a(i_o_adress), .b(8'h10), .eq(comparator_9_eq));  // open: gt, lt
  Comparator #(.mode("unsigned")) comparator_10 (.a(i_o_adress), .b(8'h12), .eq(comparator_10_eq));  // open: gt, lt
  Comparator #(.mode("unsigned")) comparator_11 (.a(i_o_adress), .b(8'h14), .eq(comparator_11_eq));  // open: gt, lt
  Comparator #(.mode("unsigned")) comparator_12 (.a(i_o_adress), .b(8'h16), .eq(comparator_12_eq));  // open: gt, lt
  Comparator #(.mode("unsigned")) comparator_13 (.a(i_o_adress), .b(8'h18), .eq(comparator_13_eq));  // open: gt, lt
  Comparator #(.mode("unsigned")) comparator_14 (.a(i_o_adress), .b(8'h1a), .eq(comparator_14_eq));  // open: gt, lt
  Comparator #(.mode("unsigned")) comparator_15 (.a(i_o_adress), .b(8'h1c), .eq(comparator_15_eq));  // open: gt, lt
  Comparator #(.mode("unsigned")) comparator_16 (.a(i_o_adress), .b(8'h1e), .eq(comparator_16_eq));  // open: gt, lt
  Comparator #(.mode("unsigned")) comparator_17 (.a(i_o_adress), .b(8'h20), .eq(comparator_17_eq));  // open: gt, lt
  Comparator #(.mode("unsigned")) comparator_18 (.a(i_o_adress), .b(8'h22), .eq(comparator_18_eq));  // open: gt, lt
  Register #(.width(16)) register_19 (
    .D(i_o_data_control), .Q(_18[15:0]), .clk(decoder_19_out0), .clr(gunsight_ans));  // open: en
  Register #(.width(16)) register_20 (
    .D(i_o_data_control), .Q(_18[31:16]), .clk(decoder_20_out0), .clr(gunsight_ans));  // open: en
  Register #(.width(16)) register_21 (
    .D(i_o_data_control), .Q(_17[15:0]), .clk(decoder_21_out0), .clr(gunsight_ans));  // open: en
  Register #(.width(16)) register_22 (
    .D(i_o_data_control), .Q(_17[31:16]), .clk(decoder_22_out0), .clr(gunsight_ans));  // open: en
  Register #(.width(16)) register_23 (
    .D(i_o_data_control), .Q(_16[15:0]), .clk(decoder_23_out0), .clr(gunsight_ans));  // open: en
  Register #(.width(16)) register_24 (
    .D(i_o_data_control), .Q(_16[31:16]), .clk(decoder_24_out0), .clr(gunsight_ans));  // open: en
  Register #(.width(16)) register_25 (
    .D(i_o_data_control), .Q(_15[15:0]), .clk(decoder_25_out0), .clr(gunsight_ans));  // open: en
  Register #(.width(16)) register_26 (
    .D(i_o_data_control), .Q(_15[31:16]), .clk(decoder_26_out0), .clr(gunsight_ans));  // open: en
  Register #(.width(16)) register_27 (
    .D(i_o_data_control), .Q(_14[15:0]), .clk(decoder_27_out0), .clr(gunsight_ans));  // open: en
  Register #(.width(16)) register_28 (
    .D(i_o_data_control), .Q(_14[31:16]), .clk(decoder_28_out0), .clr(gunsight_ans));  // open: en
  Register #(.width(16)) register_29 (
    .D(i_o_data_control), .Q(_13[15:0]), .clk(decoder_29_out0), .clr(gunsight_ans));  // open: en
  Register #(.width(16)) register_30 (
    .D(i_o_data_control), .Q(_13[31:16]), .clk(decoder_30_out0), .clr(gunsight_ans));  // open: en
  Register #(.width(16)) register_31 (
    .D(i_o_data_control), .Q(_12[15:0]), .clk(decoder_31_out0), .clr(gunsight_ans));  // open: en
  Register #(.width(16)) register_32 (
    .D(i_o_data_control), .Q(_12[31:16]), .clk(decoder_32_out0), .clr(gunsight_ans));  // open: en
  Register #(.width(16)) register_33 (
    .D(i_o_data_control), .Q(_11[15:0]), .clk(decoder_33_out0), .clr(gunsight_ans));  // open: en
  Register #(.width(16)) register_34 (
    .D(i_o_data_control), .Q(_11[31:16]), .clk(decoder_34_out0), .clr(gunsight_ans));  // open: en
  Register #(.width(16)) register_35 (
    .D(i_o_data_control), .Q(_10[15:0]), .clk(decoder_35_out0), .clr(gunsight_ans));  // open: en
  Register #(.width(16)) register_36 (
    .D(i_o_data_control), .Q(_10[31:16]), .clk(decoder_36_out0), .clr(gunsight_ans));  // open: en
  assign i_o_data_control = decoder_19_out1 ? _18[15:0] : 16'bz;  // Controlled_Buffer controlled_buffer_19
  assign i_o_data_control = decoder_20_out1 ? _18[31:16] : 16'bz;  // Controlled_Buffer controlled_buffer_20
  assign i_o_data_control = decoder_21_out1 ? _17[15:0] : 16'bz;  // Controlled_Buffer controlled_buffer_21
  assign i_o_data_control = decoder_22_out1 ? _17[31:16] : 16'bz;  // Controlled_Buffer controlled_buffer_22
  assign i_o_data_control = decoder_23_out1 ? _16[15:0] : 16'bz;  // Controlled_Buffer controlled_buffer_23
  assign i_o_data_control = decoder_24_out1 ? _16[31:16] : 16'bz;  // Controlled_Buffer controlled_buffer_24
  assign i_o_data_control = decoder_25_out1 ? _15[15:0] : 16'bz;  // Controlled_Buffer controlled_buffer_25
  assign i_o_data_control = decoder_26_out1 ? _15[31:16] : 16'bz;  // Controlled_Buffer controlled_buffer_26
  assign i_o_data_control = decoder_27_out1 ? _14[15:0] : 16'bz;  // Controlled_Buffer controlled_buffer_27
  assign i_o_data_control = decoder_28_out1 ? _14[31:16] : 16'bz;  // Controlled_Buffer controlled_buffer_28
  assign i_o_data_control = decoder_29_out1 ? _13[15:0] : 16'bz;  // Controlled_Buffer controlled_buffer_29
  assign i_o_data_control = decoder_30_out1 ? _13[31:16] : 16'bz;  // Controlled_Buffer controlled_buffer_30
  assign i_o_data_control = decoder_31_out1 ? _12[15:0] : 16'bz;  // Controlled_Buffer controlled_buffer_31
  assign i_o_data_control = decoder_32_out1 ? _12[31:16] : 16'bz;  // Controlled_Buffer controlled_buffer_32
  assign i_o_data_control = decoder_33_out1 ? _11[15:0] : 16'bz;  // Controlled_Buffer controlled_buffer_33
  assign i_o_data_control = decoder_34_out1 ? _11[31:16] : 16'bz;  // Controlled_Buffer controlled_buffer_34
  assign i_o_data_control = decoder_35_out1 ? _10[15:0] : 16'bz;  // Controlled_Buffer controlled_buffer_35
  assign i_o_data_control = decoder_36_out1 ? _10[31:16] : 16'bz;  // Controlled_Buffer controlled_buffer_36
  and _68 (_68_out, i_o_sel, comparator_19_eq);
  Decoder #(.disabled(0)) decoder_19 (.out0(decoder_19_out0), .out1(decoder_19_out1), .sel(in_out), .en(_68_out));
  and _70 (_70_out, i_o_sel, comparator_20_eq);
  Decoder #(.disabled(0)) decoder_20 (.out0(decoder_20_out0), .out1(decoder_20_out1), .sel(in_out), .en(_70_out));
  and _64 (_64_out, i_o_sel, comparator_21_eq);
  Decoder #(.disabled(0)) decoder_21 (.out0(decoder_21_out0), .out1(decoder_21_out1), .sel(in_out), .en(_64_out));
  and _66 (_66_out, i_o_sel, comparator_22_eq);
  Decoder #(.disabled(0)) decoder_22 (.out0(decoder_22_out0), .out1(decoder_22_out1), .sel(in_out), .en(_66_out));
  and _60 (_60_out, i_o_sel, comparator_23_eq);
  Decoder #(.disabled(0)) decoder_23 (.out0(decoder_23_out0), .out1(decoder_23_out1), .sel(in_out), .en(_60_out));
  and _62 (_62_out, i_o_sel, comparator_24_eq);
  Decoder #(.disabled(0)) decoder_24 (.out0(decoder_24_out0), .out1(decoder_24_out1), .sel(in_out), .en(_62_out));
  and _56 (_56_out, i_o_sel, comparator_25_eq);
  Decoder #(.disabled(0)) decoder_25 (.out0(decoder_25_out0), .out1(decoder_25_out1), .sel(in_out), .en(_56_out));
  and _58 (_58_out, i_o_sel, comparator_26_eq);
  Decoder #(.disabled(0)) decoder_26 (.out0(decoder_26_out0), .out1(decoder_26_out1), .sel(in_out), .en(_58_out));
  and _52 (_52_out, i_o_sel, comparator_27_eq);
  Decoder #(.disabled(0)) decoder_27 (.out0(decoder_27_out0), .out1(decoder_27_out1), .sel(in_out), .en(_52_out));
  and _54 (_54_out, i_o_sel, comparator_28_eq);
  Decoder #(.disabled(0)) decoder_28 (.out0(decoder_28_out0), .out1(decoder_28_out1), .sel(in_out), .en(_54_out));
  and _48 (_48_out, i_o_sel, comparator_29_eq);
  Decoder #(.disabled(0)) decoder_29 (.out0(decoder_29_out0), .out1(decoder_29_out1), .sel(in_out), .en(_48_out));
  and _50 (_50_out, i_o_sel, comparator_30_eq);
  Decoder #(.disabled(0)) decoder_30 (.out0(decoder_30_out0), .out1(decoder_30_out1), .sel(in_out), .en(_50_out));
  and _44 (_44_out, i_o_sel, comparator_31_eq);
  Decoder #(.disabled(0)) decoder_31 (.out0(decoder_31_out0), .out1(decoder_31_out1), .sel(in_out), .en(_44_out));
  and _46 (_46_out, i_o_sel, comparator_32_eq);
  Decoder #(.disabled(0)) decoder_32 (.out0(decoder_32_out0), .out1(decoder_32_out1), .sel(in_out), .en(_46_out));
  and _40 (_40_out, i_o_sel, comparator_33_eq);
  Decoder #(.disabled(0)) decoder_33 (.out0(decoder_33_out0), .out1(decoder_33_out1), .sel(in_out), .en(_40_out));
  and _42 (_42_out, i_o_sel, comparator_34_eq);
  Decoder #(.disabled(0)) decoder_34 (.out0(decoder_34_out0), .out1(decoder_34_out1), .sel(in_out), .en(_42_out));
  and _36 (_36_out, i_o_sel, comparator_35_eq);
  Decoder #(.disabled(0)) decoder_35 (.out0(decoder_35_out0), .out1(decoder_35_out1), .sel(in_out), .en(_36_out));
  and _38 (_38_out, i_o_sel, comparator_36_eq);
  Decoder #(.disabled(0)) decoder_36 (.out0(decoder_36_out0), .out1(decoder_36_out1), .sel(in_out), .en(_38_out));
  Comparator #(.mode("unsigned")) comparator_19 (.a(i_o_adress), .b(8'h44), .eq(comparator_19_eq));  // open: gt, lt
  Comparator #(.mode("unsigned")) comparator_20 (.a(i_o_adress), .b(8'h46), .eq(comparator_20_eq));  // open: gt, lt
  Comparator #(.mode("unsigned")) comparator_21 (.a(i_o_adress), .b(8'h40), .eq(comparator_21_eq));  // open: gt, lt
  Comparator #(.mode("unsigned")) comparator_22 (.a(i_o_adress), .b(8'h42), .eq(comparator_22_eq));  // open: gt, lt
  Comparator #(.mode("unsigned")) comparator_23 (.a(i_o_adress), .b(8'h3c), .eq(comparator_23_eq));  // open: gt, lt
  Comparator #(.mode("unsigned")) comparator_24 (.a(i_o_adress), .b(8'h3e), .eq(comparator_24_eq));  // open: gt, lt
  Comparator #(.mode("unsigned")) comparator_25 (.a(i_o_adress), .b(8'h38), .eq(comparator_25_eq));  // open: gt, lt
  Comparator #(.mode("unsigned")) comparator_26 (.a(i_o_adress), .b(8'h3a), .eq(comparator_26_eq));  // open: gt, lt
  Comparator #(.mode("unsigned")) comparator_27 (.a(i_o_adress), .b(8'h34), .eq(comparator_27_eq));  // open: gt, lt
  Comparator #(.mode("unsigned")) comparator_28 (.a(i_o_adress), .b(8'h36), .eq(comparator_28_eq));  // open: gt, lt
  Comparator #(.mode("unsigned")) comparator_29 (.a(i_o_adress), .b(8'h30), .eq(comparator_29_eq));  // open: gt, lt
  Comparator #(.mode("unsigned")) comparator_30 (.a(i_o_adress), .b(8'h32), .eq(comparator_30_eq));  // open: gt, lt
  Comparator #(.mode("unsigned")) comparator_31 (.a(i_o_adress), .b(8'h2c), .eq(comparator_31_eq));  // open: gt, lt
  Comparator #(.mode("unsigned")) comparator_32 (.a(i_o_adress), .b(8'h2e), .eq(comparator_32_eq));  // open: gt, lt
  Comparator #(.mode("unsigned")) comparator_33 (.a(i_o_adress), .b(8'h28), .eq(comparator_33_eq));  // open: gt, lt
  Comparator #(.mode("unsigned")) comparator_34 (.a(i_o_adress), .b(8'h2a), .eq(comparator_34_eq));  // open: gt, lt
  Comparator #(.mode("unsigned")) comparator_35 (.a(i_o_adress), .b(8'h24), .eq(comparator_35_eq));  // open: gt, lt
  Comparator #(.mode("unsigned")) comparator_36 (.a(i_o_adress), .b(8'h26), .eq(comparator_36_eq));  // open: gt, lt
  assign i_o_data_control = decoder_37_out1 ? _19[15:0] : 16'bz;  // Controlled_Buffer controlled_buffer_37
  Register #(.width(16)) register_37 (
    .D(i_o_data_control), .Q(_19[15:0]), .clk(decoder_37_out0), .clr(gunsight_ans));  // open: en
  Register #(.width(16)) register_38 (
    .D(i_o_data_control), .Q(_19[31:16]), .clk(decoder_38_out0), .clr(gunsight_ans));  // open: en
  assign i_o_data_control = decoder_39_out1 ? _20[15:0] : 16'bz;  // Controlled_Buffer controlled_buffer_38
  Register #(.width(16)) register_39 (
    .D(i_o_data_control), .Q(_20[15:0]), .clk(decoder_39_out0), .clr(gunsight_ans));  // open: en
  Register #(.width(16)) register_40 (
    .D(i_o_data_control), .Q(_20[31:16]), .clk(decoder_40_out0), .clr(gunsight_ans));  // open: en
  assign i_o_data_control = decoder_41_out1 ? _21[15:0] : 16'bz;  // Controlled_Buffer controlled_buffer_39
  Register #(.width(16)) register_41 (
    .D(i_o_data_control), .Q(_21[15:0]), .clk(decoder_41_out0), .clr(gunsight_ans));  // open: en
  Register #(.width(16)) register_42 (
    .D(i_o_data_control), .Q(_21[31:16]), .clk(decoder_42_out0), .clr(gunsight_ans));  // open: en
  assign i_o_data_control = decoder_43_out1 ? _22[15:0] : 16'bz;  // Controlled_Buffer controlled_buffer_40
  Register #(.width(16)) register_43 (
    .D(i_o_data_control), .Q(_22[15:0]), .clk(decoder_43_out0), .clr(gunsight_ans));  // open: en
  Register #(.width(16)) register_44 (
    .D(i_o_data_control), .Q(_22[31:16]), .clk(decoder_44_out0), .clr(gunsight_ans));  // open: en
  assign i_o_data_control = decoder_45_out1 ? _23[15:0] : 16'bz;  // Controlled_Buffer controlled_buffer_41
  Register #(.width(16)) register_45 (
    .D(i_o_data_control), .Q(_23[15:0]), .clk(decoder_45_out0), .clr(gunsight_ans));  // open: en
  Register #(.width(16)) register_46 (
    .D(i_o_data_control), .Q(_23[31:16]), .clk(decoder_46_out0), .clr(gunsight_ans));  // open: en
  assign i_o_data_control = decoder_47_out1 ? _24[15:0] : 16'bz;  // Controlled_Buffer controlled_buffer_42
  Register #(.width(16)) register_47 (
    .D(i_o_data_control), .Q(_24[15:0]), .clk(decoder_47_out0), .clr(gunsight_ans));  // open: en
  Register #(.width(16)) register_48 (
    .D(i_o_data_control), .Q(_24[31:16]), .clk(decoder_48_out0), .clr(gunsight_ans));  // open: en
  assign i_o_data_control = decoder_49_out1 ? _25[15:0] : 16'bz;  // Controlled_Buffer controlled_buffer_43
  Register #(.width(16)) register_49 (
    .D(i_o_data_control), .Q(_25[15:0]), .clk(decoder_49_out0), .clr(gunsight_ans));  // open: en
  Register #(.width(16)) register_50 (
    .D(i_o_data_control), .Q(_25[31:16]), .clk(decoder_50_out0), .clr(gunsight_ans));  // open: en
  assign i_o_data_control = decoder_51_out1 ? _26[15:0] : 16'bz;  // Controlled_Buffer controlled_buffer_44
  Register #(.width(16)) register_51 (
    .D(i_o_data_control), .Q(_26[15:0]), .clk(decoder_51_out0), .clr(gunsight_ans));  // open: en
  Register #(.width(16)) register_52 (
    .D(i_o_data_control), .Q(_26[31:16]), .clk(decoder_52_out0), .clr(gunsight_ans));  // open: en
  assign i_o_data_control = decoder_53_out1 ? _27[15:0] : 16'bz;  // Controlled_Buffer controlled_buffer_45
  Register #(.width(16)) register_53 (
    .D(i_o_data_control), .Q(_27[15:0]), .clk(decoder_53_out0), .clr(gunsight_ans));  // open: en
  Register #(.width(16)) register_54 (
    .D(i_o_data_control), .Q(_27[31:16]), .clk(decoder_54_out0), .clr(gunsight_ans));  // open: en
  assign i_o_data_control = decoder_55_out1 ? _28[15:0] : 16'bz;  // Controlled_Buffer controlled_buffer_46
  Register #(.width(16)) register_55 (
    .D(i_o_data_control), .Q(_28[15:0]), .clk(decoder_55_out0), .clr(gunsight_ans));  // open: en
  Register #(.width(16)) register_56 (
    .D(i_o_data_control), .Q(_28[31:16]), .clk(decoder_56_out0), .clr(gunsight_ans));  // open: en
  Decoder #(.disabled(0)) decoder_37 (.out0(decoder_37_out0), .out1(decoder_37_out1), .sel(in_out), .en(_72_out));
  Decoder #(.disabled(0)) decoder_38 (.out0(decoder_38_out0), .out1(decoder_38_out1), .sel(in_out), .en(_74_out));
  assign i_o_data_control = decoder_38_out1 ? _19[31:16] : 16'bz;  // Controlled_Buffer controlled_buffer_47
  Decoder #(.disabled(0)) decoder_39 (.out0(decoder_39_out0), .out1(decoder_39_out1), .sel(in_out), .en(_76_out));
  Decoder #(.disabled(0)) decoder_40 (.out0(decoder_40_out0), .out1(decoder_40_out1), .sel(in_out), .en(_78_out));
  assign i_o_data_control = decoder_40_out1 ? _20[31:16] : 16'bz;  // Controlled_Buffer controlled_buffer_48
  Decoder #(.disabled(0)) decoder_41 (.out0(decoder_41_out0), .out1(decoder_41_out1), .sel(in_out), .en(_80_out));
  Decoder #(.disabled(0)) decoder_42 (.out0(decoder_42_out0), .out1(decoder_42_out1), .sel(in_out), .en(_82_out));
  assign i_o_data_control = decoder_42_out1 ? _21[31:16] : 16'bz;  // Controlled_Buffer controlled_buffer_49
  Decoder #(.disabled(0)) decoder_43 (.out0(decoder_43_out0), .out1(decoder_43_out1), .sel(in_out), .en(_84_out));
  Decoder #(.disabled(0)) decoder_44 (.out0(decoder_44_out0), .out1(decoder_44_out1), .sel(in_out), .en(_86_out));
  assign i_o_data_control = decoder_44_out1 ? _22[31:16] : 16'bz;  // Controlled_Buffer controlled_buffer_50
  Decoder #(.disabled(0)) decoder_45 (.out0(decoder_45_out0), .out1(decoder_45_out1), .sel(in_out), .en(_88_out));
  Decoder #(.disabled(0)) decoder_46 (.out0(decoder_46_out0), .out1(decoder_46_out1), .sel(in_out), .en(_90_out));
  assign i_o_data_control = decoder_46_out1 ? _23[31:16] : 16'bz;  // Controlled_Buffer controlled_buffer_51
  Decoder #(.disabled(0)) decoder_47 (.out0(decoder_47_out0), .out1(decoder_47_out1), .sel(in_out), .en(_92_out));
  Decoder #(.disabled(0)) decoder_48 (.out0(decoder_48_out0), .out1(decoder_48_out1), .sel(in_out), .en(_94_out));
  assign i_o_data_control = decoder_48_out1 ? _24[31:16] : 16'bz;  // Controlled_Buffer controlled_buffer_52
  Decoder #(.disabled(0)) decoder_49 (.out0(decoder_49_out0), .out1(decoder_49_out1), .sel(in_out), .en(_96_out));
  Decoder #(.disabled(0)) decoder_50 (.out0(decoder_50_out0), .out1(decoder_50_out1), .sel(in_out), .en(_98_out));
  assign i_o_data_control = decoder_50_out1 ? _25[31:16] : 16'bz;  // Controlled_Buffer controlled_buffer_53
  Decoder #(.disabled(0)) decoder_51 (.out0(decoder_51_out0), .out1(decoder_51_out1), .sel(in_out), .en(_100_out));
  Decoder #(.disabled(0)) decoder_52 (.out0(decoder_52_out0), .out1(decoder_52_out1), .sel(in_out), .en(_102_out));
  assign i_o_data_control = decoder_52_out1 ? _26[31:16] : 16'bz;  // Controlled_Buffer controlled_buffer_54
  Decoder #(.disabled(0)) decoder_53 (.out0(decoder_53_out0), .out1(decoder_53_out1), .sel(in_out), .en(_104_out));
  Decoder #(.disabled(0)) decoder_54 (.out0(decoder_54_out0), .out1(decoder_54_out1), .sel(in_out), .en(_106_out));
  assign i_o_data_control = decoder_54_out1 ? _27[31:16] : 16'bz;  // Controlled_Buffer controlled_buffer_55
  Decoder #(.disabled(0)) decoder_55 (.out0(decoder_55_out0), .out1(decoder_55_out1), .sel(in_out), .en(_108_out));
  Decoder #(.disabled(0)) decoder_56 (.out0(decoder_56_out0), .out1(decoder_56_out1), .sel(in_out), .en(_110_out));
  assign i_o_data_control = decoder_56_out1 ? _28[31:16] : 16'bz;  // Controlled_Buffer controlled_buffer_56
  and _72 (_72_out, i_o_sel, comparator_37_eq);
  and _74 (_74_out, i_o_sel, comparator_38_eq);
  and _76 (_76_out, i_o_sel, comparator_39_eq);
  and _78 (_78_out, i_o_sel, comparator_40_eq);
  and _80 (_80_out, i_o_sel, comparator_41_eq);
  and _82 (_82_out, i_o_sel, comparator_42_eq);
  and _84 (_84_out, i_o_sel, comparator_43_eq);
  and _86 (_86_out, i_o_sel, comparator_44_eq);
  and _88 (_88_out, i_o_sel, comparator_45_eq);
  and _90 (_90_out, i_o_sel, comparator_46_eq);
  and _92 (_92_out, i_o_sel, comparator_47_eq);
  and _94 (_94_out, i_o_sel, comparator_48_eq);
  and _96 (_96_out, i_o_sel, comparator_49_eq);
  and _98 (_98_out, i_o_sel, comparator_50_eq);
  and _100 (_100_out, i_o_sel, comparator_51_eq);
  and _102 (_102_out, i_o_sel, comparator_52_eq);
  and _104 (_104_out, i_o_sel, comparator_53_eq);
  and _106 (_106_out, i_o_sel, comparator_54_eq);
  and _108 (_108_out, i_o_sel, comparator_55_eq);
  and _110 (_110_out, i_o_sel, comparator_56_eq);
  Comparator #(.mode("unsigned")) comparator_37 (.a(i_o_adress), .b(8'h48), .eq(comparator_37_eq));  // open: gt, lt
  Comparator #(.mode("unsigned")) comparator_38 (.a(i_o_adress), .b(8'h4a), .eq(comparator_38_eq));  // open: gt, lt
  Comparator #(.mode("unsigned")) comparator_39 (.a(i_o_adress), .b(8'h4c), .eq(comparator_39_eq));  // open: gt, lt
  Comparator #(.mode("unsigned")) comparator_40 (.a(i_o_adress), .b(8'h4e), .eq(comparator_40_eq));  // open: gt, lt
  Comparator #(.mode("unsigned")) comparator_41 (.a(i_o_adress), .b(8'h50), .eq(comparator_41_eq));  // open: gt, lt
  Comparator #(.mode("unsigned")) comparator_42 (.a(i_o_adress), .b(8'h52), .eq(comparator_42_eq));  // open: gt, lt
  Comparator #(.mode("unsigned")) comparator_43 (.a(i_o_adress), .b(8'h54), .eq(comparator_43_eq));  // open: gt, lt
  Comparator #(.mode("unsigned")) comparator_44 (.a(i_o_adress), .b(8'h56), .eq(comparator_44_eq));  // open: gt, lt
  Comparator #(.mode("unsigned")) comparator_45 (.a(i_o_adress), .b(8'h58), .eq(comparator_45_eq));  // open: gt, lt
  Comparator #(.mode("unsigned")) comparator_46 (.a(i_o_adress), .b(8'h5a), .eq(comparator_46_eq));  // open: gt, lt
  Comparator #(.mode("unsigned")) comparator_47 (.a(i_o_adress), .b(8'h5c), .eq(comparator_47_eq));  // open: gt, lt
  Comparator #(.mode("unsigned")) comparator_48 (.a(i_o_adress), .b(8'h5e), .eq(comparator_48_eq));  // open: gt, lt
  Comparator #(.mode("unsigned")) comparator_49 (.a(i_o_adress), .b(8'h60), .eq(comparator_49_eq));  // open: gt, lt
  Comparator #(.mode("unsigned")) comparator_50 (.a(i_o_adress), .b(8'h62), .eq(comparator_50_eq));  // open: gt, lt
  Comparator #(.mode("unsigned")) comparator_51 (.a(i_o_adress), .b(8'h64), .eq(comparator_51_eq));  // open: gt, lt
  Comparator #(.mode("unsigned")) comparator_52 (.a(i_o_adress), .b(8'h66), .eq(comparator_52_eq));  // open: gt, lt
  Comparator #(.mode("unsigned")) comparator_53 (.a(i_o_adress), .b(8'h68), .eq(comparator_53_eq));  // open: gt, lt
  Comparator #(.mode("unsigned")) comparator_54 (.a(i_o_adress), .b(8'h6a), .eq(comparator_54_eq));  // open: gt, lt
  Comparator #(.mode("unsigned")) comparator_55 (.a(i_o_adress), .b(8'h6c), .eq(comparator_55_eq));  // open: gt, lt
  Comparator #(.mode("unsigned")) comparator_56 (.a(i_o_adress), .b(8'h6e), .eq(comparator_56_eq));  // open: gt, lt
  Pull_Resistor #(.pull(1)) pull_resistor_1 (.node(pull_resistor_1_node));
  not not_1 (not_1_out, pull_resistor_1_node);
  not not_2 (not_2_out, decoder_57_out1);
  nor nor_1 (nor_1_out, not_1_out, pull_resistor_1_node);
  nor nor_2 (nor_2_out, not_2_out, decoder_57_out1);
  Transistor #(.\type ("n")) transistor_1 (.in(1'b0), .out(pull_resistor_1_node), .gate(and_1_out));
  and and_1 (and_1_out, keyboard_active, or_1_out);
  Comparator #(.width(7), .mode("unsigned")) comparator_57 (
    .a(7'b1110111), .b(keyboard), .eq(comparator_57_eq));  // open: gt, lt
  Comparator #(.width(7), .mode("unsigned")) comparator_58 (
    .a(7'b1100001), .b(keyboard), .eq(comparator_58_eq));  // open: gt, lt
  Comparator #(.width(7), .mode("unsigned")) comparator_59 (
    .a(7'b1110011), .b(keyboard), .eq(comparator_59_eq));  // open: gt, lt
  Comparator #(.width(7), .mode("unsigned")) comparator_60 (
    .a(7'b1100100), .b(keyboard), .eq(comparator_60_eq));  // open: gt, lt
  S_R_Flip_Flop #(.trigger("low")) s_r_ff_1 (
    .S(nor_1_out), .clk(1'b0), .R(nor_2_out), .Q(s_r_ff_1_q[7]));  // open: Qn, preset, reset, en
  Register #(.width(7), .trigger("falling")) register_57 (
    .D(keyboard), .Q(register_57_q), .clk(pull_resistor_1_node));  // open: en, clr
  or or_1 (or_1_out, comparator_57_eq, comparator_58_eq, comparator_59_eq, comparator_60_eq);
  Pull_Resistor pull_resistor_2 (.node(s_r_ff_1_q[8]));
  assign i_o_data_control = decoder_57_out1 ? {s_r_ff_1_q, register_57_q} : 16'bz;  // Controlled_Buffer controlled_buffer_57
  Pull_Resistor pull_resistor_3 (.node(s_r_ff_1_q[9]));
  Pull_Resistor pull_resistor_4 (.node(s_r_ff_1_q[10]));
  Pull_Resistor pull_resistor_5 (.node(s_r_ff_1_q[11]));
  Pull_Resistor pull_resistor_6 (.node(s_r_ff_1_q[12]));
  Pull_Resistor pull_resistor_7 (.node(s_r_ff_1_q[13]));
  Pull_Resistor pull_resistor_8 (.node(s_r_ff_1_q[14]));
  Pull_Resistor pull_resistor_9 (.node(s_r_ff_1_q[15]));
  Register #(.width(16)) register_58 (
    .D(i_o_data_control), .Q(_32[15:0]), .clk(decoder_58_out0), .clr(gunsight_ans));  // open: en
  Register #(.width(16)) register_59 (
    .D(i_o_data_control), .Q(_32[31:16]), .clk(decoder_59_out0), .clr(gunsight_ans));  // open: en
  Register #(.width(16)) register_60 (
    .D(i_o_data_control), .Q(_31[15:0]), .clk(decoder_60_out0), .clr(gunsight_ans));  // open: en
  Register #(.width(16)) register_61 (
    .D(i_o_data_control), .Q(_31[31:16]), .clk(decoder_61_out0), .clr(gunsight_ans));  // open: en
  Register #(.width(16)) register_62 (
    .D(i_o_data_control), .Q(_30[15:0]), .clk(decoder_62_out0), .clr(gunsight_ans));  // open: en
  Register #(.width(16)) register_63 (
    .D(i_o_data_control), .Q(_30[31:16]), .clk(decoder_63_out0), .clr(gunsight_ans));  // open: en
  Register #(.width(16)) register_64 (
    .D(i_o_data_control), .Q(_29[15:0]), .clk(decoder_64_out0), .clr(gunsight_ans));  // open: en
  Register #(.width(16)) register_65 (
    .D(i_o_data_control), .Q(_29[31:16]), .clk(decoder_65_out0), .clr(gunsight_ans));  // open: en
  // Probe on i_o_data_control
  assign i_o_data_control = decoder_58_out1 ? _32[15:0] : 16'bz;  // Controlled_Buffer controlled_buffer_58
  assign i_o_data_control = decoder_59_out1 ? _32[31:16] : 16'bz;  // Controlled_Buffer controlled_buffer_59
  assign i_o_data_control = decoder_60_out1 ? _31[15:0] : 16'bz;  // Controlled_Buffer controlled_buffer_60
  assign i_o_data_control = decoder_61_out1 ? _31[31:16] : 16'bz;  // Controlled_Buffer controlled_buffer_61
  assign i_o_data_control = decoder_62_out1 ? _30[15:0] : 16'bz;  // Controlled_Buffer controlled_buffer_62
  assign i_o_data_control = decoder_63_out1 ? _30[31:16] : 16'bz;  // Controlled_Buffer controlled_buffer_63
  assign i_o_data_control = decoder_64_out1 ? _29[15:0] : 16'bz;  // Controlled_Buffer controlled_buffer_64
  assign i_o_data_control = decoder_65_out1 ? _29[31:16] : 16'bz;  // Controlled_Buffer controlled_buffer_65
  and _176 (_176_out, i_o_sel, comparator_61_eq);
  Decoder #(.disabled(0)) decoder_57 (.out1(decoder_57_out1), .sel(in_out), .en(_176_out));  // open: out0
  and _124 (_124_out, i_o_sel, comparator_62_eq);
  Decoder #(.disabled(0)) decoder_58 (.out0(decoder_58_out0), .out1(decoder_58_out1), .sel(in_out), .en(_124_out));
  and _126 (_126_out, i_o_sel, comparator_63_eq);
  Decoder #(.disabled(0)) decoder_59 (.out0(decoder_59_out0), .out1(decoder_59_out1), .sel(in_out), .en(_126_out));
  and _120 (_120_out, i_o_sel, comparator_64_eq);
  Decoder #(.disabled(0)) decoder_60 (.out0(decoder_60_out0), .out1(decoder_60_out1), .sel(in_out), .en(_120_out));
  and _122 (_122_out, i_o_sel, comparator_65_eq);
  Decoder #(.disabled(0)) decoder_61 (.out0(decoder_61_out0), .out1(decoder_61_out1), .sel(in_out), .en(_122_out));
  and _116 (_116_out, i_o_sel, comparator_66_eq);
  Decoder #(.disabled(0)) decoder_62 (.out0(decoder_62_out0), .out1(decoder_62_out1), .sel(in_out), .en(_116_out));
  and _118 (_118_out, i_o_sel, comparator_67_eq);
  Decoder #(.disabled(0)) decoder_63 (.out0(decoder_63_out0), .out1(decoder_63_out1), .sel(in_out), .en(_118_out));
  and _112 (_112_out, i_o_sel, comparator_68_eq);
  Decoder #(.disabled(0)) decoder_64 (.out0(decoder_64_out0), .out1(decoder_64_out1), .sel(in_out), .en(_112_out));
  and _114 (_114_out, i_o_sel, comparator_69_eq);
  Decoder #(.disabled(0)) decoder_65 (.out0(decoder_65_out0), .out1(decoder_65_out1), .sel(in_out), .en(_114_out));
  Comparator #(.mode("unsigned")) comparator_61 (.a(i_o_adress), .b(8'hb0), .eq(comparator_61_eq));  // open: gt, lt
  Comparator #(.mode("unsigned")) comparator_62 (.a(i_o_adress), .b(8'h7c), .eq(comparator_62_eq));  // open: gt, lt
  Comparator #(.mode("unsigned")) comparator_63 (.a(i_o_adress), .b(8'h7e), .eq(comparator_63_eq));  // open: gt, lt
  Comparator #(.mode("unsigned")) comparator_64 (.a(i_o_adress), .b(8'h78), .eq(comparator_64_eq));  // open: gt, lt
  Comparator #(.mode("unsigned")) comparator_65 (.a(i_o_adress), .b(8'h7a), .eq(comparator_65_eq));  // open: gt, lt
  Comparator #(.mode("unsigned")) comparator_66 (.a(i_o_adress), .b(8'h74), .eq(comparator_66_eq));  // open: gt, lt
  Comparator #(.mode("unsigned")) comparator_67 (.a(i_o_adress), .b(8'h76), .eq(comparator_67_eq));  // open: gt, lt
  Comparator #(.mode("unsigned")) comparator_68 (.a(i_o_adress), .b(8'h70), .eq(comparator_68_eq));  // open: gt, lt
  Comparator #(.mode("unsigned")) comparator_69 (.a(i_o_adress), .b(8'h72), .eq(comparator_69_eq));  // open: gt, lt

  assign out = i_o_data_control;
endmodule

module shot (
  input  [31:0] _1_bird,
  input  [31:0] _2_bird,
  input  [31:0] _3_bird,
  input  [31:0] _4_bird,
  input  [31:0] _5_bird,
  input  [31:0] _6_bird,
  input  [31:0] _7_bird,
  input  [31:0] _8_bird,
  input  [31:0] _1_gunsight,
  input  [31:0] _2_gunsight,
  input  [31:0] _3_gunsight,
  input  [31:0] _4_gunsight,
  input  [31:0] _5_gunsight,
  input  [31:0] _6_gunsight,
  input  [31:0] _7_gunsight,
  input  [31:0] _8_gunsight,
  input  [31:0] _9_bird,
  input  [31:0] _10_bird,
  input  [31:0] _11_bird,
  input  [31:0] _12_bird,
  input  [31:0] _13_bird,
  input  [31:0] _14_bird,
  input  [31:0] _15_bird,
  input  [31:0] _16_bird,
  input  [31:0] _9_gunsight,
  input  [31:0] _10_gunsight,
  input  [31:0] _11_gunsight,
  input  [31:0] _12_gunsight,
  input  [31:0] _13_gunsight,
  input  [31:0] _14_gunsight,
  input  [31:0] _15_gunsight,
  input  [31:0] _16_gunsight,
  input  [31:0] _17_bird,
  input  [31:0] _18_bird,
  input  [31:0] _19_bird,
  input  [31:0] _20_bird,
  input  [31:0] _21_bird,
  input  [31:0] _22_bird,
  input  [31:0] _23_bird,
  input  [31:0] _24_bird,
  input  [31:0] _17_gunsight,
  input  [31:0] _18_gunsight,
  input  [31:0] _19_gunsight,
  input  [31:0] _20_gunsight,
  input  [31:0] _21_gunsight,
  input  [31:0] _22_gunsight,
  input  [31:0] _23_gunsight,
  input  [31:0] _24_gunsight,
  input  [31:0] _25_bird,
  input  [31:0] _26_bird,
  input  [31:0] _27_bird,
  input  [31:0] _28_bird,
  input  [31:0] _29_bird,
  input  [31:0] _30_bird,
  input  [31:0] _31_bird,
  input  [31:0] _32_bird,
  input  [31:0] _25_gunsight,
  input  [31:0] _26_gunsight,
  input  [31:0] _27_gunsight,
  input  [31:0] _28_gunsight,
  input  [31:0] _29_gunsight,
  input  [31:0] _30_gunsight,
  input  [31:0] _31_gunsight,
  input  [31:0] _32_gunsight,
  input  bird_ans,
  input  shot,
  input  clear,
  output [31:0] _1,
  output [31:0] _2,
  output [31:0] _3,
  output [31:0] _4,
  output [31:0] _5,
  output [31:0] _6,
  output [31:0] _7,
  output [31:0] _8,
  output [31:0] _9,
  output [31:0] _10,
  output [31:0] _11,
  output [31:0] _12,
  output [31:0] _13,
  output [31:0] _14,
  output [31:0] _15,
  output [31:0] _16,
  output [31:0] _17,
  output [31:0] _18,
  output [31:0] _19,
  output [31:0] _20,
  output [31:0] _21,
  output [31:0] _22,
  output [31:0] _23,
  output [31:0] _24,
  output KILL,
  output [31:0] _25,
  output [31:0] _26,
  output [31:0] _27,
  output [31:0] _28,
  output [31:0] _29,
  output [31:0] _30,
  output [31:0] _31,
  output [31:0] _32,
  output reset_bird,
  output too_many_misses,
  output [3:0] misses
);

  wire _1_shot, _2_shot, _3_shot, _4_shot, _5_shot, _6_shot, _7_shot, _8_shot, _9_shot, _10_shot, _11_shot,
       _12_shot, _13_shot, _14_shot, _15_shot, _16_shot, _17_shot, _18_shot, _19_shot, _20_shot, _21_shot,
       _22_shot, _23_shot, _24_shot, _25_shot, _26_shot, _27_shot, _28_shot, _29_shot, _30_shot, _31_shot,
       _32_shot, buffer_1_out, not_1_out, not_2_out, not_3_out, or_13_out;
  wire [15:0] counter_1_q, counter_2_q;
  wire [15:4] subtractor_1_out;
  wire [31:0] and_1_out, and_2_out, and_3_out, and_4_out, and_5_out, and_6_out, and_7_out, and_8_out,
       and_10_out, and_11_out, and_12_out, and_13_out, and_15_out, and_16_out, and_17_out, and_18_out,
       and_19_out, and_20_out, and_21_out, and_22_out, and_23_out, and_24_out, and_25_out, and_26_out,
       and_27_out, and_28_out, and_29_out, and_30_out, and_31_out, and_32_out, and_33_out, and_34_out;

  assign and_1_out = _1_bird & _1_gunsight;  // AND_Gate and_1, 32 bits wide
  assign and_2_out = _9_bird & _9_gunsight;  // AND_Gate and_2, 32 bits wide
  assign and_3_out = _17_bird & _17_gunsight;  // AND_Gate and_3, 32 bits wide
  assign and_4_out = _25_bird & _25_gunsight;  // AND_Gate and_4, 32 bits wide
  Comparator #(.width(32), .mode("unsigned")) comparator_1 (
    .a({32{1'b0}}), .b(and_1_out), .lt(_1_shot));  // open: gt, eq
  assign _1 = _1_bird | _1_gunsight;  // OR_Gate or_1, 32 bits wide
  Comparator #(.width(32), .mode("unsigned")) comparator_2 (
    .a({32{1'b0}}), .b(and_2_out), .lt(_9_shot));  // open: gt, eq
  assign _9 = _9_bird | _9_gunsight;  // OR_Gate or_2, 32 bits wide
  Comparator #(.width(32), .mode("unsigned")) comparator_3 (
    .a({32{1'b0}}), .b(and_3_out), .lt(_17_shot));  // open: gt, eq
  assign _17 = _17_bird | _17_gunsight;  // OR_Gate or_3, 32 bits wide
  Comparator #(.width(32), .mode("unsigned")) comparator_4 (
    .a({32{1'b0}}), .b(and_4_out), .lt(_25_shot));  // open: gt, eq
  assign _25 = _25_bird | _25_gunsight;  // OR_Gate or_4, 32 bits wide
  Pull_Resistor pull_resistor_1 (.node(bird_ans));
  not not_1 (not_1_out, bird_ans);
  assign and_5_out = _2_bird & _2_gunsight;  // AND_Gate and_5, 32 bits wide
  assign and_6_out = _10_bird & _10_gunsight;  // AND_Gate and_6, 32 bits wide
  assign and_7_out = _18_bird & _18_gunsight;  // AND_Gate and_7, 32 bits wide
  assign and_8_out = _26_bird & _26_gunsight;  // AND_Gate and_8, 32 bits wide
  not not_2 (not_2_out, bird_ans);
  not not_3 (not_3_out, not_2_out);
  and and_9 (reset_bird, not_1_out, not_3_out);
  Comparator #(.width(32), .mode("unsigned")) comparator_5 (
    .a({32{1'b0}}), .b(and_5_out), .lt(_2_shot));  // open: gt, eq
  assign _2 = _2_bird | _2_gunsight;  // OR_Gate or_5, 32 bits wide
  Comparator #(.width(32), .mode("unsigned")) comparator_6 (
    .a({32{1'b0}}), .b(and_6_out), .lt(_10_shot));  // open: gt, eq
  assign _10 = _10_bird | _10_gunsight;  // OR_Gate or_6, 32 bits wide
  Comparator #(.width(32), .mode("unsigned")) comparator_7 (
    .a({32{1'b0}}), .b(and_7_out), .lt(_18_shot));  // open: gt, eq
  assign _18 = _18_bird | _18_gunsight;  // OR_Gate or_7, 32 bits wide
  Comparator #(.width(32), .mode("unsigned")) comparator_8 (
    .a({32{1'b0}}), .b(and_8_out), .lt(_26_shot));  // open: gt, eq
  assign _26 = _26_bird | _26_gunsight;  // OR_Gate or_8, 32 bits wide
  assign and_10_out = _3_bird & _3_gunsight;  // AND_Gate and_10, 32 bits wide
  assign and_11_out = _11_bird & _11_gunsight;  // AND_Gate and_11, 32 bits wide
  assign and_12_out = _19_bird & _19_gunsight;  // AND_Gate and_12, 32 bits wide
  assign and_13_out = _27_bird & _27_gunsight;  // AND_Gate and_13, 32 bits wide
  and and_14 (KILL, or_13_out, shot);
  Counter #(.width(16), .max('hffff), .ongoal("stay")) counter_1 (
    .Q(counter_1_q), .clk(KILL), .clr(clear));  // open: load, D, count, carry
  Comparator #(.width(32), .mode("unsigned")) comparator_9 (
    .a({32{1'b0}}), .b(and_10_out), .lt(_3_shot));  // open: gt, eq
  assign _3 = _3_bird | _3_gunsight;  // OR_Gate or_9, 32 bits wide
  Comparator #(.width(32), .mode("unsigned")) comparator_10 (
    .a({32{1'b0}}), .b(and_11_out), .lt(_11_shot));  // open: gt, eq
  assign _11 = _11_bird | _11_gunsight;  // OR_Gate or_10, 32 bits wide
  Comparator #(.width(32), .mode("unsigned")) comparator_11 (
    .a({32{1'b0}}), .b(and_12_out), .lt(_19_shot));  // open: gt, eq
  assign _19 = _19_bird | _19_gunsight;  // OR_Gate or_11, 32 bits wide
  Comparator #(.width(32), .mode("unsigned")) comparator_12 (
    .a({32{1'b0}}), .b(and_13_out), .lt(_27_shot));  // open: gt, eq
  assign _27 = _27_bird | _27_gunsight;  // OR_Gate or_12, 32 bits wide
  or or_13 (or_13_out, _1_shot, _2_shot, _3_shot, _4_shot, _5_shot, _6_shot, _7_shot, _8_shot, _9_shot, _10_shot, _11_shot, _12_shot, _13_shot, _14_shot, _15_shot, _16_shot, _17_shot, _18_shot, _19_shot, _20_shot, _21_shot, _22_shot, _23_shot, _24_shot, _25_shot, _26_shot, _27_shot, _28_shot, _29_shot, _30_shot, _31_shot, _32_shot);
  Counter #(.width(16), .max('hffff), .ongoal("stay")) counter_2 (
    .Q(counter_2_q), .clk(buffer_1_out), .clr(clear));  // open: load, D, count, carry
  buf buffer_1 (buffer_1_out, shot);
  assign and_15_out = _4_bird & _4_gunsight;  // AND_Gate and_15, 32 bits wide
  assign and_16_out = _12_bird & _12_gunsight;  // AND_Gate and_16, 32 bits wide
  assign and_17_out = _20_bird & _20_gunsight;  // AND_Gate and_17, 32 bits wide
  assign and_18_out = _28_bird & _28_gunsight;  // AND_Gate and_18, 32 bits wide
  Subtractor #(.width(16)) subtractor_1 (
    .a(counter_2_q), .b(counter_1_q), .out({subtractor_1_out, misses}));  // open: bin, bout
  Comparator #(.width(32), .mode("unsigned")) comparator_13 (
    .a({32{1'b0}}), .b(and_15_out), .lt(_4_shot));  // open: gt, eq
  assign _4 = _4_bird | _4_gunsight;  // OR_Gate or_14, 32 bits wide
  Comparator #(.width(32), .mode("unsigned")) comparator_14 (
    .a({32{1'b0}}), .b(and_16_out), .lt(_12_shot));  // open: gt, eq
  assign _12 = _12_bird | _12_gunsight;  // OR_Gate or_15, 32 bits wide
  Comparator #(.width(32), .mode("unsigned")) comparator_15 (
    .a({32{1'b0}}), .b(and_17_out), .lt(_20_shot));  // open: gt, eq
  assign _20 = _20_bird | _20_gunsight;  // OR_Gate or_16, 32 bits wide
  Comparator #(.width(32), .mode("unsigned")) comparator_16 (
    .a({32{1'b0}}), .b(and_18_out), .lt(_28_shot));  // open: gt, eq
  assign _28 = _28_bird | _28_gunsight;  // OR_Gate or_17, 32 bits wide
  Pull_Resistor pull_resistor_2 (.node(too_many_misses));
  Comparator #(.width(16), .mode("unsigned")) comparator_17 (
    .a({subtractor_1_out, misses}), .b(16'h5), .eq(too_many_misses));  // open: gt, lt
  Comparator #(.width(32), .mode("unsigned")) comparator_18 (
    .a({32{1'b0}}), .b(and_19_out), .lt(_5_shot));  // open: gt, eq
  assign and_19_out = _5_bird & _5_gunsight;  // AND_Gate and_19, 32 bits wide
  assign _5 = _5_bird | _5_gunsight;  // OR_Gate or_18, 32 bits wide
  Comparator #(.width(32), .mode("unsigned")) comparator_19 (
    .a({32{1'b0}}), .b(and_20_out), .lt(_13_shot));  // open: gt, eq
  assign and_20_out = _13_bird & _13_gunsight;  // AND_Gate and_20, 32 bits wide
  assign _13 = _13_bird | _13_gunsight;  // OR_Gate or_19, 32 bits wide
  Comparator #(.width(32), .mode("unsigned")) comparator_20 (
    .a({32{1'b0}}), .b(and_21_out), .lt(_21_shot));  // open: gt, eq
  assign _21 = _21_bird | _21_gunsight;  // OR_Gate or_20, 32 bits wide
  assign and_21_out = _21_bird & _21_gunsight;  // AND_Gate and_21, 32 bits wide
  Comparator #(.width(32), .mode("unsigned")) comparator_21 (
    .a({32{1'b0}}), .b(and_22_out), .lt(_29_shot));  // open: gt, eq
  assign _29 = _29_bird | _29_gunsight;  // OR_Gate or_21, 32 bits wide
  assign and_22_out = _29_bird & _29_gunsight;  // AND_Gate and_22, 32 bits wide
  Comparator #(.width(32), .mode("unsigned")) comparator_22 (
    .a({32{1'b0}}), .b(and_23_out), .lt(_6_shot));  // open: gt, eq
  assign _6 = _6_bird | _6_gunsight;  // OR_Gate or_22, 32 bits wide
  assign and_23_out = _6_bird & _6_gunsight;  // AND_Gate and_23, 32 bits wide
  Comparator #(.width(32), .mode("unsigned")) comparator_23 (
    .a({32{1'b0}}), .b(and_24_out), .lt(_14_shot));  // open: gt, eq
  assign _14 = _14_bird | _14_gunsight;  // OR_Gate or_23, 32 bits wide
  assign and_24_out = _14_bird & _14_gunsight;  // AND_Gate and_24, 32 bits wide
  Comparator #(.width(32), .mode("unsigned")) comparator_24 (
    .a({32{1'b0}}), .b(and_25_out), .lt(_22_shot));  // open: gt, eq
  assign _22 = _22_bird | _22_gunsight;  // OR_Gate or_24, 32 bits wide
  assign and_25_out = _22_bird & _22_gunsight;  // AND_Gate and_25, 32 bits wide
  Comparator #(.width(32), .mode("unsigned")) comparator_25 (
    .a({32{1'b0}}), .b(and_26_out), .lt(_30_shot));  // open: gt, eq
  assign and_26_out = _30_bird & _30_gunsight;  // AND_Gate and_26, 32 bits wide
  assign _30 = _30_bird | _30_gunsight;  // OR_Gate or_25, 32 bits wide
  assign and_27_out = _7_bird & _7_gunsight;  // AND_Gate and_27, 32 bits wide
  assign and_28_out = _15_bird & _15_gunsight;  // AND_Gate and_28, 32 bits wide
  assign and_29_out = _23_bird & _23_gunsight;  // AND_Gate and_29, 32 bits wide
  assign and_30_out = _31_bird & _31_gunsight;  // AND_Gate and_30, 32 bits wide
  Comparator #(.width(32), .mode("unsigned")) comparator_26 (
    .a({32{1'b0}}), .b(and_27_out), .lt(_7_shot));  // open: gt, eq
  assign _7 = _7_bird | _7_gunsight;  // OR_Gate or_26, 32 bits wide
  Comparator #(.width(32), .mode("unsigned")) comparator_27 (
    .a({32{1'b0}}), .b(and_28_out), .lt(_15_shot));  // open: gt, eq
  assign _15 = _15_bird | _15_gunsight;  // OR_Gate or_27, 32 bits wide
  Comparator #(.width(32), .mode("unsigned")) comparator_28 (
    .a({32{1'b0}}), .b(and_29_out), .lt(_23_shot));  // open: gt, eq
  assign _23 = _23_bird | _23_gunsight;  // OR_Gate or_28, 32 bits wide
  Comparator #(.width(32), .mode("unsigned")) comparator_29 (
    .a({32{1'b0}}), .b(and_30_out), .lt(_31_shot));  // open: gt, eq
  assign _31 = _31_bird | _31_gunsight;  // OR_Gate or_29, 32 bits wide
  Comparator #(.width(32), .mode("unsigned")) comparator_30 (
    .a({32{1'b0}}), .b(and_31_out), .lt(_8_shot));  // open: gt, eq
  assign and_31_out = _8_bird & _8_gunsight;  // AND_Gate and_31, 32 bits wide
  assign _8 = _8_bird | _8_gunsight;  // OR_Gate or_30, 32 bits wide
  Comparator #(.width(32), .mode("unsigned")) comparator_31 (
    .a({32{1'b0}}), .b(and_32_out), .lt(_16_shot));  // open: gt, eq
  assign and_32_out = _16_bird & _16_gunsight;  // AND_Gate and_32, 32 bits wide
  assign _16 = _16_bird | _16_gunsight;  // OR_Gate or_31, 32 bits wide
  Comparator #(.width(32), .mode("unsigned")) comparator_32 (
    .a({32{1'b0}}), .b(and_33_out), .lt(_24_shot));  // open: gt, eq
  assign _24 = _24_bird | _24_gunsight;  // OR_Gate or_32, 32 bits wide
  assign and_33_out = _24_bird & _24_gunsight;  // AND_Gate and_33, 32 bits wide
  Comparator #(.width(32), .mode("unsigned")) comparator_33 (
    .a({32{1'b0}}), .b(and_34_out), .lt(_32_shot));  // open: gt, eq
  assign _32 = _32_bird | _32_gunsight;  // OR_Gate or_33, 32 bits wide
  assign and_34_out = _32_bird & _32_gunsight;  // AND_Gate and_34, 32 bits wide
endmodule
