// Logisim project IncompatibleData.circ as structural Verilog: 1 circuit, main circuit main
module main (
);

  wire and_1_out, clock_1_out, comparator_1_eq, not_1_out;
  wire [15:0] adder_1_out, register_1_q;
  wire [15:1] undriven;

  Clock clock_1 (.out(clock_1_out));
  not not_1 (not_1_out, comparator_1_eq);
  Comparator #(.width(16)) comparator_1 (.a(16'h4e20), .b(register_1_q), .eq(comparator_1_eq));  // open: gt, lt
  and and_1 (and_1_out, clock_1_out, not_1_out);
  Adder #(.width(16)) adder_1 (.a(16'h1), .b(register_1_q), .out(adder_1_out));  // open: cin, cout
  // Probe on register_1_q
  Register #(.width(16)) register_1 (.D(adder_1_out), .Q(register_1_q), .clk(and_1_out));  // open: en, clr
  Register #(.width(16)) register_2 (.D({undriven, 1'b1}), .clk(and_1_out));  // open: en, Q, clr
  // Pins of 1 and 16 bits meet at {undriven, 1'b1}
endmodule
