// Logisim project Oscillating.circ as structural Verilog: 1 circuit, main circuit main
module main (
);

  wire and_1_out, and_2_out, clock_1_out, comparator_1_eq, not_1_out, not_2_out;
  wire [15:0] adder_1_out, register_1_q;

  Clock clock_1 (.out(clock_1_out));
  not not_1 (not_1_out, comparator_1_eq);
  Comparator #(.width(16)) comparator_1 (.a(16'h4e20), .b(register_1_q), .eq(comparator_1_eq));  // open: gt, lt
  and and_1 (and_1_out, clock_1_out, not_1_out);
  Adder #(.width(16)) adder_1 (.a(16'h1), .b(register_1_q), .out(adder_1_out));  // open: cin, cout
  // Probe on register_1_q
  Register #(.width(16)) register_1 (.D(adder_1_out), .Q(register_1_q), .clk(and_1_out));  // open: en, clr
  and and_2 (and_2_out, and_1_out, not_2_out);
  not not_2 (not_2_out, and_2_out);
endmodule
