// Logisim project fibonacci.circ as structural Verilog: 3 circuits, main circuit main
module main (
);

  wire clock_1_out, spliter_1_out_2;
  wire [15:0] cdm_16_1_t;

  LED led_1 (.in(spliter_1_out_2));
  Clock clock_1 (.out(clock_1_out));
  CdM_16 cdm_16_1 (.t(cdm_16_1_t), .clock(clock_1_out));
  spliter spliter_1 (.out_2(spliter_1_out_2), .in_1(cdm_16_1_t));
endmodule

module CdM_16 (
  input  clock,
  output [15:0] t
);

  wire cdm16_1_data_ins_prime, cdm16_1_mem, code, data, not_1_out, read_write, word;
  wire [15:0] cdm16_1_address, cdm16_1_data_out, controlled_buffer_1_out, controlled_buffer_2_out;

  cdm16 cdm16_1 (
    .mem(cdm16_1_mem), .data_ins_prime(cdm16_1_data_ins_prime), .rd_wr_prime(read_write),
    .address(cdm16_1_address), .word(word), .R6(t), .data_out(cdm16_1_data_out),
    .data_in(controlled_buffer_2_out), .clock(clock));  // open: EXC, exc_vec, IRQ, int_vec, hold, R0, R1, R2, R3, R4, R5, FP, PC, PS, SP, status, fetch, IAck
  assign controlled_buffer_1_out = not_1_out ? cdm16_1_data_out : 16'bz;  // Controlled_Buffer controlled_buffer_1
  not not_1 (not_1_out, read_write);
  assign controlled_buffer_2_out = read_write ? controlled_buffer_1_out : 16'bz;  // Controlled_Buffer controlled_buffer_2
  Decoder #(.disabled(0)) decoder_1 (.out0(code), .out1(data), .sel(cdm16_1_data_ins_prime), .en(cdm16_1_mem));
  // ROM rom_1: pin names not known; wires that end beside it: cdm16_1_address, code, word, controlled_buffer_1_out
  // RAM ram_1: pin names not known; wires that end beside it: cdm16_1_address, word, data, clock, read_write, controlled_buffer_1_out
endmodule

module spliter (
  input  [15:0] in_1,
  output out_2
);


  assign out_2 = in_1[0];
endmodule
