// Logisim project test.circ as structural Verilog: 1 circuit, main circuit main
module main (
  output bus_0
);

  wire and_1_out, clock_1_out, not_1_out;

  Clock clock_1 (.out(clock_1_out));
  not not_1 (not_1_out, clock_1_out);
  and and_1 (and_1_out, clock_1_out, not_1_out);
  or or_1 (bus_0, and_1_out, clock_1_out);
endmodule
