// Logisim project test_nesting.circ as structural Verilog: 6 circuits, main circuit main
module main (
  output bus_0
);

  wire clock_1_out;

  Clock clock_1 (.out(clock_1_out));
  _5 u_5_1 (.bus_0(clock_1_out), .bus_0_2(bus_0));
endmodule

module _1 (
  input  bus_0,
  output bus_0_2
);

  wire and_1_out, not_1_out;

  not not_1 (not_1_out, bus_0);
  and and_1 (and_1_out, bus_0, not_1_out);
  or or_1 (bus_0_2, and_1_out, bus_0);
endmodule

module _2 (
  input  bus_0,
  output bus_0_2
);

  _1 u_1_1 (.bus_0(bus_0), .bus_0_2(bus_0_2));
endmodule

module _3 (
  input  bus_0,
  output bus_0_2
);

  _2 u_2_1 (.bus_0(bus_0), .bus_0_2(bus_0_2));
endmodule

module _4 (
  input  bus_0,
  output bus_0_2
);

  _3 u_3_1 (.bus_0(bus_0), .bus_0_2(bus_0_2));
endmodule

module _5 (
  input  bus_0,
  output bus_0_2
);

  _4 u_4_1 (.bus_0(bus_0), .bus_0_2(bus_0_2));
endmodule
